// Logisim project Osnova8_CPU.circ as structural Verilog: 7 circuits, main circuit CPU
module CPU (
  input  DIn0,
  input  DIn1,
  input  DIn2,
  input  DIn3,
  input  DIn4,
  input  DIn5,
  input  DIn6,
  input  DIn7,
  input  CndX,
  input  IntX,
  output DOut0,
  output DOut1,
  output DOut2,
  output DOut3,
  output DOut4,
  output Dout5,
  output DOut6,
  output DOut7
);

  wire Arg0, Arg1, Arg2, Arg3, Carry, EqH, EqL, Equ, Int, IntM, Neg, Odd, part_pf_1_cout, PRA0, PWA0, PWA1;

  PART_SCTPS part_sctps_1 (
    .DIn0(DIn0), .DIn1(DIn1), .DIn2(DIn2), .DIn3(DIn3), .WA0(PWA0), .WA1(PWA1), .RA0(PRA0), .RA1(PRA0),
    .DIn4(DIn4), .DIn5(DIn5), .DIn6(DIn6), .DIn7(DIn7), .Int(Int), .ACT_INT(IntM), .PRA0(PRA0), .PRA1(PRA0),
    .PWA0(PWA0), .PWA1(PWA1), .DOut0(DOut7), .DOut1(DOut6), .DOut2(Dout5), .DOut3(DOut4), .DOut4(DOut3),
    .Dout5(DOut2), .DOut6(DOut1), .DOut7(DOut0));  // open: MPC, MPS, SFW, PSW, OE, IntR
  PART_ALU part_alu_1 (
    .DIn0(DIn0), .DIn1(DIn1), .DIn2(DIn2), .DIn3(DIn3), .DIn4(DIn4), .DIn5(DIn5), .DIn6(DIn6), .DIn7(DIn7),
    .EQ_L(EqL), .CARRY(Carry), .EQ_H(EqH), .ODD(Odd), .NEG(Neg), .DOut0(DOut0), .DOut1(DOut1), .DOut2(DOut2),
    .DOut3(DOut3), .DOut4(DOut4), .Dout5(Dout5), .DOut6(DOut6), .DOut7(DOut7));  // open: DVR4, ARG_ALU, OPC_RC, ARG_RC, OPC_RESR, ARG_RESR, OPC_RA, OPC_RB, DVR0, DVR1, DVR2, DVR3, DVR5
  PART_PF part_pf_1 (
    .WA0(PWA0), .WA1(PWA1), .RA0(PRA0), .RA1(PRA0), .DIn0(DIn0), .DIn1(DIn1), .DIn2(DIn2), .DIn3(DIn3),
    .DIn4(DIn4), .DIn5(DIn5), .DIn6(DIn6), .DIn7(DIn7), .DOut0(DOut7), .DOut1(DOut6), .DOut2(Dout5),
    .DOut3(DOut4), .DOut4(DOut3), .Dout5(DOut2), .DOut6(DOut1), .DOut7(DOut0), .COut(part_pf_1_cout));  // open: WE, RE, OE, CIn, Step, MInc, MSet0, MSet1
  PART_PF part_pf_2 (
    .WA0(PWA0), .WA1(PWA1), .RA0(PRA0), .RA1(PRA0), .CIn(part_pf_1_cout), .DIn0(DIn0), .DIn1(DIn1),
    .DIn2(DIn2), .DIn3(DIn3), .DIn4(DIn4), .DIn5(DIn5), .DIn6(DIn6), .DIn7(DIn7), .DOut0(DOut0),
    .DOut1(DOut1), .DOut2(DOut2), .DOut3(DOut3), .DOut4(DOut4), .Dout5(Dout5), .DOut6(DOut6), .DOut7(DOut7));  // open: WE, RE, OE, Step, MInc, MSet0, MSet1, COut
  PART_IEU part_ieu_1 (
    .DIn0(DIn0), .DIn1(DIn1), .DIn2(DIn2), .DIn3(DIn3), .DIn4(DIn4), .DIn5(DIn5), .DIn6(DIn6), .DIn7(DIn7),
    .DOut0(DOut0), .DOut1(DOut1), .DOut2(DOut2), .DOut3(DOut3), .DOut4(DOut4), .Dout5(Dout5), .DOut6(DOut6),
    .DOut7(DOut7), .Arg3(Arg3), .Arg0(Arg0), .Arg1(Arg1), .Arg2(Arg2));  // open: IR, DVRLW, DVRHW, DVRR, ACT_OPC, ACT_ARG, DVROE, OPC_DVRH, OPC_RA, OPC_RB, OPC_RC, OPC_INTSI, OPC_INTSX, OPC_INTE, JMP_SENSE, ARG_ALU, ARG_SFPS, ARG_RC, ARG_PFL, ARG_PFH, ARG_RESR, ARG_ADD, ARG_DVR, OPC_JMP, OPC_SF, OPC_PS, OPC_PFL, OPC_PFH, OPC_RESR, OPC_ADD, OPC_DVRR, OPC_DVRL
  PART_CU part_cu_1 ();  // open: En0, En1, Clk, ACT_JMP, ARG_ADD, ACT_PC, ACT_ARG, EvenCyc, Step0, Step1, Step2, Step3, Step4, Step5, Step6, Step7, ACT_INC_STAGE, ACT_ADD_R
  PART_CMBL part_cmbl_1 (
    .EQU(Equ), .CNDX(CndX), .INTM(IntM), .CARRY(Carry), .NEG(Neg), .ODD(Odd), .S0(Arg0), .S1(Arg1),
    .S2(Arg2), .INTX(IntX), .EQ_L(EqL), .EQ_H(EqH), .INT(Int), .EQ(Equ));  // open: OPC_PFL, INC_STAGE, OPC_PFH, OPC_JMP, JMP_SENSE, ACT_ARG, ARG3, OPC_INTSI, ACT_INCPL, ACT_INCPL_N, ACT_INCPH, ACT_INCPH_N, ACT_JMP, ACT_PC, ACT_PC_BRIDGE, ACT_INST, ACT_INST_BRIDGE, PFL_CIN

  // Notes on the sheet:
  //   DIn0: pull=up
  //   DIn1: pull=up
  //   DIn2: pull=up
  //   DIn3: pull=up
  //   DIn4: pull=up
  //   DIn5: pull=up
  //   DIn6: pull=up
  //   DIn7: pull=up
  //   CndX: pull=up
  //   IntX: pull=up
endmodule

module PART_ALU (
  input  DIn0,
  input  DIn1,
  input  DIn2,
  input  DIn3,
  input  DIn4,
  input  DIn5,
  input  DIn6,
  input  DIn7,
  input  OPC_RA,
  input  ARG_ALU,
  input  DVR4,
  input  OPC_RB,
  input  DVR0,
  input  DVR1,
  input  DVR2,
  input  DVR3,
  input  DVR5,
  input  OPC_RC,
  input  ARG_RC,
  input  OPC_RESR,
  input  ARG_RESR,
  output ODD,
  output DOut0,
  output DOut1,
  output DOut2,
  output DOut3,
  output DOut4,
  output Dout5,
  output EQ_L,
  output DOut6,
  output DOut7,
  output NEG,
  output CARRY,
  output EQ_H
);

  wire ic_74181_1_cout, ic_74181_1_f1, ic_74181_1_f2, ic_74181_1_f3, ic_74181_2_f0, ic_74181_2_f1,
       ic_74181_2_f2, ic_74374_1_o0, ic_74374_1_o1, ic_74374_1_o2, ic_74374_1_o3, ic_74374_1_o4,
       ic_74374_1_o5, ic_74374_1_o6, ic_74374_1_o7, ic_74374_2_o0, ic_74374_2_o1, ic_74374_2_o2,
       ic_74374_2_o3, ic_74374_2_o4, ic_74374_2_o5, ic_74374_2_o6, ic_74374_2_o7;

  IC_74374 ic_74374_1 (
    .D0(DIn0), .D1(DIn1), .D2(DIn2), .D3(DIn3), .D4(DIn4), .D5(DIn5), .D6(DIn6), .D7(DIn7), .Cp(OPC_RA),
    .OE(1'b0), .O0(ic_74374_1_o0), .O1(ic_74374_1_o1), .O2(ic_74374_1_o2), .O3(ic_74374_1_o3),
    .O4(ic_74374_1_o4), .O5(ic_74374_1_o5), .O6(ic_74374_1_o6), .O7(ic_74374_1_o7));
  IC_74374 ic_74374_2 (
    .D0(DIn0), .D1(DIn1), .D2(DIn2), .D3(DIn3), .D4(DIn4), .D5(DIn5), .D6(DIn6), .D7(DIn7), .Cp(OPC_RB),
    .OE(1'b0), .O0(ic_74374_2_o0), .O1(ic_74374_2_o1), .O2(ic_74374_2_o2), .O3(ic_74374_2_o3),
    .O4(ic_74374_2_o4), .O5(ic_74374_2_o5), .O6(ic_74374_2_o6), .O7(ic_74374_2_o7));
  IC_74374 ic_74374_3 (
    .D0(DIn0), .D1(DIn1), .D2(DIn2), .D3(DIn3), .D4(DIn4), .D5(DIn5), .D6(DIn6), .D7(DIn7), .Cp(OPC_RC),
    .OE(ARG_RC), .O0(DOut0), .O1(DOut1), .O2(DOut2), .O3(DOut3), .O4(DOut4), .O5(Dout5), .O6(DOut6),
    .O7(DOut7));
  IC_74374 ic_74374_4 (
    .D0(DIn0), .D1(DIn1), .D2(DIn2), .D3(DIn3), .D4(DIn4), .D5(DIn5), .D6(DIn6), .D7(DIn7), .Cp(OPC_RESR),
    .OE(ARG_RESR), .O0(DOut0), .O1(DOut1), .O2(DOut2), .O3(DOut3), .O4(DOut4), .O5(Dout5), .O6(DOut6),
    .O7(DOut7));
  IC_74181 ic_74181_1 (
    .B0(ic_74374_2_o0), .A0(ic_74374_1_o0), .S3(DVR3), .S2(DVR2), .S1(DVR1), .S0(DVR0), .CIn(DVR4), .M(DVR5),
    .A1(ic_74374_1_o1), .B1(ic_74374_2_o1), .A2(ic_74374_1_o2), .B2(ic_74374_2_o2), .A3(ic_74374_1_o3),
    .B3(ic_74374_2_o3), .F0(ODD), .F1(ic_74181_1_f1), .F2(ic_74181_1_f2), .COut(ic_74181_1_cout),
    .AEQB(EQ_L), .F3(ic_74181_1_f3));  // open: G, P
  IC_74181 ic_74181_2 (
    .B0(ic_74374_2_o4), .A0(ic_74374_1_o4), .S3(DVR3), .S2(DVR2), .S1(DVR1), .S0(DVR0),
    .CIn(ic_74181_1_cout), .M(DVR5), .A1(ic_74374_1_o5), .B1(ic_74374_2_o5), .A2(ic_74374_1_o6),
    .B2(ic_74374_2_o6), .A3(ic_74374_1_o7), .B3(ic_74374_2_o7), .F0(ic_74181_2_f0), .F1(ic_74181_2_f1),
    .F2(ic_74181_2_f2), .COut(CARRY), .AEQB(EQ_H), .F3(NEG));  // open: G, P
  IC_74541 ic_74541_1 (
    .A0(ODD), .A1(ic_74181_1_f1), .A2(ic_74181_1_f2), .A3(ic_74181_1_f3), .A4(ic_74181_2_f0),
    .A5(ic_74181_2_f1), .A6(ic_74181_2_f2), .A7(NEG), .G1(ARG_ALU), .G2(1'b0), .Y0(DOut0), .Y1(DOut1),
    .Y2(DOut2), .Y3(DOut3), .Y4(DOut4), .Y5(Dout5), .Y6(DOut6), .Y7(DOut7));

  // Notes on the sheet:
  //   DVR4: pull=up
  //   ARG_ALU: pull=up
  //   DIn0: pull=up
  //   DIn1: pull=up
  //   DIn2: pull=up
  //   DIn3: pull=up
  //   DIn4: pull=up
  //   DIn5: pull=up
  //   DIn6: pull=up
  //   DIn7: pull=up
  //   OPC_RC: pull=up
  //   ARG_RC: pull=up
  //   OPC_RESR: pull=up
  //   ARG_RESR: pull=up
  //   OPC_RA: pull=up
  //   OPC_RB: pull=up
  //   DVR0: pull=up
  //   DVR1: pull=up
  //   DVR2: pull=up
  //   DVR3: pull=up
  //   DVR5: pull=up
endmodule

module PART_PF (
  input  CIn,
  input  Step,
  input  OE,
  input  MInc,
  input  DIn0,
  input  DIn1,
  input  DIn2,
  input  DIn3,
  input  DIn4,
  input  DIn5,
  input  DIn6,
  input  DIn7,
  input  MSet0,
  input  WA0,
  input  MSet1,
  input  WA1,
  input  WE,
  input  RA0,
  input  RA1,
  input  RE,
  output DOut0,
  output DOut1,
  output DOut2,
  output DOut3,
  output DOut4,
  output Dout5,
  output DOut6,
  output DOut7,
  output COut
);

  wire ic_74283_1_c4, ic_74283_1_o1, ic_74283_1_o2, ic_74283_1_o3, ic_74283_1_o4, ic_74283_2_o1,
       ic_74283_2_o2, ic_74283_2_o3, ic_74283_2_o4, ic_74374_1_o0, ic_74374_1_o1, ic_74374_1_o2,
       ic_74374_1_o3, ic_74374_1_o4, ic_74374_1_o5, ic_74374_1_o6, ic_74374_1_o7, ic_74670_1_q1,
       ic_74670_1_q2, ic_74670_1_q3, ic_74670_1_q4, ic_74670_2_q1, ic_74670_2_q2, ic_74670_2_q3,
       ic_74670_2_q4;

  IC_74283 ic_74283_1 (
    .A1(ic_74670_1_q4), .B1(1'b0), .A2(ic_74670_1_q1), .B2(1'b0), .A3(ic_74670_1_q2), .B3(1'b0),
    .A4(ic_74670_1_q3), .B4(1'b0), .C0(CIn), .O1(ic_74283_1_o1), .O2(ic_74283_1_o2), .O3(ic_74283_1_o3),
    .O4(ic_74283_1_o4), .C4(ic_74283_1_c4));
  IC_74283 ic_74283_2 (
    .A1(ic_74670_2_q4), .B1(1'b0), .A2(ic_74670_2_q1), .B2(1'b0), .A3(ic_74670_2_q2), .B3(1'b0),
    .A4(ic_74670_2_q3), .B4(1'b0), .C0(ic_74283_1_c4), .O1(ic_74283_2_o1), .O2(ic_74283_2_o2),
    .O3(ic_74283_2_o3), .O4(ic_74283_2_o4), .C4(COut));
  IC_74374 ic_74374_1 (
    .D0(ic_74283_1_o1), .D1(ic_74283_1_o2), .D2(ic_74283_1_o3), .D3(ic_74283_1_o4), .D4(ic_74283_2_o1),
    .D5(ic_74283_2_o2), .D6(ic_74283_2_o3), .D7(ic_74283_2_o4), .Cp(Step), .OE(MInc), .O0(ic_74374_1_o0),
    .O1(ic_74374_1_o1), .O2(ic_74374_1_o2), .O3(ic_74374_1_o3), .O4(ic_74374_1_o4), .O5(ic_74374_1_o5),
    .O6(ic_74374_1_o6), .O7(ic_74374_1_o7));
  IC_74541 ic_74541_1 (
    .A0(DIn0), .A1(DIn1), .A2(DIn2), .A3(DIn3), .A4(DIn4), .A5(DIn5), .A6(DIn6), .A7(DIn7), .G1(MSet0),
    .G2(MSet1), .Y0(ic_74374_1_o0), .Y1(ic_74374_1_o1), .Y2(ic_74374_1_o2), .Y3(ic_74374_1_o3),
    .Y4(ic_74374_1_o4), .Y5(ic_74374_1_o5), .Y6(ic_74374_1_o6), .Y7(ic_74374_1_o7));
  IC_74670 ic_74670_1 (
    .D2(ic_74374_1_o2), .D3(ic_74374_1_o3), .D4(ic_74374_1_o0), .WE(WE), .WA0(WA0), .WA1(WA1), .RE(RE),
    .RA0(RA0), .RA1(RA1), .D1(ic_74374_1_o1), .Q2(ic_74670_1_q2), .Q3(ic_74670_1_q3), .Q4(ic_74670_1_q4),
    .Q1(ic_74670_1_q1));
  IC_74670 ic_74670_2 (
    .D2(ic_74374_1_o6), .D3(ic_74374_1_o7), .D4(ic_74374_1_o4), .WE(WE), .WA0(WA0), .WA1(WA1), .RE(RE),
    .RA0(RA0), .RA1(RA1), .D1(ic_74374_1_o5), .Q2(ic_74670_2_q2), .Q3(ic_74670_2_q3), .Q4(ic_74670_2_q4),
    .Q1(ic_74670_2_q1));
  IC_74541 ic_74541_2 (
    .A0(ic_74670_1_q4), .A1(ic_74670_1_q1), .A2(ic_74670_1_q2), .A3(ic_74670_1_q3), .A4(ic_74670_2_q4),
    .A5(ic_74670_2_q1), .A6(ic_74670_2_q2), .A7(ic_74670_2_q3), .G1(OE), .G2(1'b0), .Y0(DOut0), .Y1(DOut1),
    .Y2(DOut2), .Y3(DOut3), .Y4(DOut4), .Y5(Dout5), .Y6(DOut6), .Y7(DOut7));

  // Notes on the sheet:
  //   WA0: pull=up
  //   WA1: pull=up
  //   WE: pull=up
  //   RA0: pull=up
  //   RA1: pull=up
  //   RE: pull=up
  //   OE: pull=up
  //   CIn: pull=up
  //   Step: pull=up
  //   MInc: pull=up
  //   DIn0: pull=up
  //   DIn1: pull=up
  //   DIn2: pull=up
  //   DIn3: pull=up
  //   DIn4: pull=up
  //   DIn5: pull=up
  //   DIn6: pull=up
  //   DIn7: pull=up
  //   MSet0: pull=up
  //   MSet1: pull=up
endmodule

module PART_CU (
  input  En0,
  input  En1,
  input  Clk,
  input  ACT_JMP,
  input  ARG_ADD,
  input  ACT_PC,
  output Step0,
  output Step1,
  output Step2,
  output EvenCyc,
  output Step3,
  output Step4,
  output Step5,
  output Step6,
  output Step7,
  output ACT_ARG,
  output ACT_INC_STAGE,
  output ACT_ADD_R
);

  wire ic_7408_3_y, ic_74161_1_q0, ic_74161_1_q1, ic_74161_1_q2;

  IC_74161 ic_74161_1 (
    .EnT(En1), .EnP(En0), .D0(1'b1), .D1(1'b1), .D2(1'b1), .D3(1'b1), .Load(1'b1), .Cp(Clk), .Clr(1'b1),
    .Q0(ic_74161_1_q0), .Q1(ic_74161_1_q1), .Q2(ic_74161_1_q2), .Q3(EvenCyc));  // open: TC
  IC_74138 ic_74138_1 (
    .E3(1'b1), .E2(1'b0), .E1(1'b0), .A2(ic_74161_1_q2), .A1(ic_74161_1_q1), .A0(ic_74161_1_q0), .O2(Step2),
    .O3(Step3), .O4(Step4), .O5(Step5), .O6(Step6), .O7(Step7), .O0(Step0), .O1(Step1));
  IC_7408 ic_7408_1 (.A(Step6), .B(ACT_JMP), .Y(ACT_INC_STAGE));
  IC_7408 ic_7408_2 (.A(ARG_ADD), .B(ACT_PC), .Y(ACT_ADD_R));
  IC_7408 ic_7408_3 (.A(Step2), .B(Step3), .Y(ic_7408_3_y));
  IC_7408 ic_7408_4 (.A(ic_7408_3_y), .B(Step4), .Y(ACT_ARG));

  // Notes on the sheet:
  //   En0: pull=up
  //   En1: pull=up
  //   Clk: pull=up
  //   ACT_JMP: pull=up
  //   ARG_ADD: pull=up
  //   ACT_PC: pull=up
endmodule

module PART_IEU (
  input  DVRLW,
  input  DVROE,
  input  DVRHW,
  input  DVRR,
  input  DIn0,
  input  DIn1,
  input  ACT_ARG,
  input  DIn2,
  input  DIn3,
  input  DIn4,
  input  DIn5,
  input  DIn6,
  input  DIn7,
  input  IR,
  input  ACT_OPC,
  output Arg0,
  output Arg1,
  output Arg2,
  output Arg3,
  output DOut0,
  output DOut1,
  output DOut2,
  output DOut3,
  output DOut4,
  output Dout5,
  output DOut6,
  output DOut7,
  output ARG_ALU,
  output ARG_SFPS,
  output ARG_RC,
  output ARG_PFL,
  output ARG_PFH,
  output ARG_RESR,
  output ARG_ADD,
  output ARG_DVR,
  output OPC_JMP,
  output OPC_SF,
  output OPC_PS,
  output OPC_PFL,
  output OPC_PFH,
  output OPC_RESR,
  output OPC_ADD,
  output OPC_DVRR,
  output OPC_DVRL,
  output OPC_DVRH,
  output OPC_RA,
  output OPC_RB,
  output OPC_RC,
  output OPC_INTSI,
  output OPC_INTSX,
  output OPC_INTE,
  output JMP_SENSE
);

  wire ic_74161_1_q0, ic_74161_1_q1, ic_74161_1_q2, ic_74161_1_q3, ic_74161_2_q0, ic_74161_2_q1,
       ic_74161_2_q2, ic_74161_2_q3, ic_74374_1_o4, ic_74374_1_o5, ic_74374_1_o6, ic_74374_1_o7;

  IC_74374 ic_74374_1 (
    .D0(DIn0), .D1(DIn1), .D2(DIn2), .D3(DIn3), .D4(DIn4), .D5(DIn5), .D6(DIn6), .D7(DIn7), .Cp(IR),
    .OE(1'b0), .O0(Arg0), .O1(Arg1), .O2(Arg2), .O3(Arg3), .O4(ic_74374_1_o4), .O5(ic_74374_1_o5),
    .O6(ic_74374_1_o6), .O7(ic_74374_1_o7));
  IC_74161 ic_74161_1 (
    .EnT(1'b0), .EnP(1'b0), .D0(Arg0), .D1(Arg1), .D2(Arg2), .D3(Arg3), .Load(1'b0), .Cp(DVRLW), .Clr(DVRR),
    .Q0(ic_74161_1_q0), .Q1(ic_74161_1_q1), .Q2(ic_74161_1_q2), .Q3(ic_74161_1_q3));  // open: TC
  IC_74161 ic_74161_2 (
    .EnT(1'b0), .EnP(1'b0), .D0(Arg0), .D1(Arg1), .D2(Arg2), .D3(Arg3), .Load(1'b0), .Cp(DVRHW), .Clr(DVRR),
    .Q0(ic_74161_2_q0), .Q1(ic_74161_2_q1), .Q2(ic_74161_2_q2), .Q3(ic_74161_2_q3));  // open: TC
  IC_74138 ic_74138_1 (
    .E3(1'b1), .E2(Arg3), .E1(ACT_ARG), .A2(Arg2), .A1(Arg1), .A0(Arg0), .O2(ARG_RC), .O3(ARG_PFL),
    .O4(ARG_PFH), .O5(ARG_RESR), .O6(ARG_ADD), .O7(ARG_DVR), .O0(ARG_ALU), .O1(ARG_SFPS));
  IC_74138 ic_74138_2 (
    .E3(1'b1), .E2(ic_74374_1_o7), .E1(ACT_OPC), .A2(ic_74374_1_o6), .A1(ic_74374_1_o5), .A0(ic_74374_1_o4),
    .O2(OPC_PS), .O3(OPC_PFL), .O4(OPC_PFH), .O5(OPC_RESR), .O6(OPC_ADD), .O7(OPC_DVRR), .O0(OPC_JMP),
    .O1(OPC_SF));
  IC_74138 ic_74138_3 (
    .E3(ic_74374_1_o7), .E2(1'b0), .E1(ACT_OPC), .A2(ic_74374_1_o6), .A1(ic_74374_1_o5), .A0(ic_74374_1_o4),
    .O2(OPC_RA), .O3(OPC_RB), .O4(OPC_RC), .O5(OPC_INTSI), .O6(OPC_INTSX), .O7(OPC_INTE), .O0(OPC_DVRL),
    .O1(OPC_DVRH));
  IC_74138 ic_74138_4 (
    .E3(1'b1), .E2(ic_74374_1_o7), .E1(1'b0), .A2(ic_74374_1_o6), .A1(ic_74374_1_o5), .A0(ic_74374_1_o4),
    .O0(JMP_SENSE));  // open: O2, O3, O4, O5, O6, O7, O1
  IC_74541 ic_74541_1 (
    .A0(ic_74161_1_q0), .A1(ic_74161_1_q1), .A2(ic_74161_1_q2), .A3(ic_74161_1_q3), .A4(ic_74161_2_q0),
    .A5(ic_74161_2_q1), .A6(ic_74161_2_q2), .A7(ic_74161_2_q3), .G1(DVROE), .G2(1'b0), .Y0(DOut0),
    .Y1(DOut1), .Y2(DOut2), .Y3(DOut3), .Y4(DOut4), .Y5(Dout5), .Y6(DOut6), .Y7(DOut7));

  // Notes on the sheet:
  //   DIn0: pull=up
  //   DIn1: pull=up
  //   DIn2: pull=up
  //   DIn3: pull=up
  //   DIn4: pull=up
  //   DIn5: pull=up
  //   DIn6: pull=up
  //   DIn7: pull=up
  //   IR: pull=up
  //   DVRLW: pull=up
  //   DVRHW: pull=up
  //   DVRR: pull=up
  //   ACT_OPC: pull=up
  //   ACT_ARG: pull=up
  //   DVROE: pull=up
endmodule

module PART_SCTPS (
  input  DIn0,
  input  DIn1,
  input  DIn2,
  input  DIn3,
  input  WA0,
  input  WA1,
  input  SFW,
  input  Int,
  input  RA0,
  input  OE,
  input  MPC,
  input  RA1,
  input  IntR,
  input  DIn4,
  input  DIn5,
  input  DIn6,
  input  DIn7,
  input  PSW,
  input  MPS,
  output ACT_INT,
  output DOut0,
  output PRA0,
  output DOut1,
  output PRA1,
  output DOut2,
  output PWA0,
  output DOut3,
  output PWA1,
  output DOut4,
  output Dout5,
  output DOut6,
  output DOut7
);

  wire ic_74374_1_o4, ic_74374_1_o5, ic_74374_1_o6, ic_74374_1_o7, ic_74670_1_q1, ic_74670_1_q2,
       ic_74670_1_q3, ic_74670_1_q4;

  IC_74670 ic_74670_1 (
    .D2(DIn2), .D3(DIn3), .D4(DIn0), .WE(SFW), .WA0(WA0), .WA1(WA1), .RE(1'b0), .RA0(RA0), .RA1(RA1),
    .D1(DIn1), .Q2(ic_74670_1_q2), .Q3(ic_74670_1_q3), .Q4(ic_74670_1_q4), .Q1(ic_74670_1_q1));
  IC_74374 ic_74374_1 (
    .D0(1'b1), .D1(1'b1), .D2(1'b1), .D3(1'b1), .D4(DIn4), .D5(DIn5), .D6(DIn6), .D7(DIn7), .Cp(PSW),
    .OE(1'b0), .O4(ic_74374_1_o4), .O5(ic_74374_1_o5), .O6(ic_74374_1_o6), .O7(ic_74374_1_o7));  // open: O0, O1, O2, O3
  IC_74541 ic_74541_1 (
    .A0(ic_74670_1_q4), .A1(ic_74670_1_q1), .A2(ic_74670_1_q2), .A3(ic_74670_1_q3), .A4(ic_74374_1_o4),
    .A5(ic_74374_1_o5), .A6(ic_74374_1_o6), .A7(ic_74374_1_o7), .G1(OE), .G2(1'b0), .Y0(DOut0), .Y1(DOut1),
    .Y2(DOut2), .Y3(DOut3), .Y4(DOut4), .Y5(Dout5), .Y6(DOut6), .Y7(DOut7));
  IC_74161 ic_74161_1 (
    .EnT(1'b1), .EnP(1'b1), .D0(1'b1), .D1(1'b1), .D2(1'b1), .D3(1'b1), .Load(1'b0), .Cp(Int), .Clr(IntR),
    .Q0(ACT_INT));  // open: Q1, Q2, Q3, TC
  IC_74541 ic_74541_2 (
    .A0(1'b0), .A1(ACT_INT), .A2(1'b0), .A3(ACT_INT), .A4(1'b1), .A5(1'b1), .A6(1'b1), .A7(1'b1), .G1(MPC),
    .G2(1'b0), .Y0(PRA0), .Y1(PRA1), .Y2(PWA0), .Y3(PWA1));  // open: Y4, Y5, Y6, Y7
  IC_74541 ic_74541_3 (
    .A0(ic_74374_1_o4), .A1(ic_74374_1_o5), .A2(ic_74374_1_o6), .A3(ic_74374_1_o7), .A4(1'b1), .A5(1'b1),
    .A6(1'b1), .A7(1'b1), .G1(MPS), .G2(1'b0), .Y0(PRA0), .Y1(PRA1), .Y2(PWA0), .Y3(PWA1));  // open: Y4, Y5, Y6, Y7

  // Notes on the sheet:
  //   MPC: pull=up
  //   MPS: pull=up
  //   DIn0: pull=up
  //   DIn1: pull=up
  //   DIn2: pull=up
  //   DIn3: pull=up
  //   WA0: pull=up
  //   WA1: pull=up
  //   SFW: pull=up
  //   RA0: pull=up
  //   RA1: pull=up
  //   DIn4: pull=up
  //   DIn5: pull=up
  //   DIn6: pull=up
  //   DIn7: pull=up
  //   PSW: pull=up
  //   OE: pull=up
  //   Int: pull=up
  //   IntR: pull=up
endmodule

module PART_CMBL (
  input  EQU,
  input  CNDX,
  input  INTX,
  input  INTM,
  input  OPC_INTSI,
  input  CARRY,
  input  NEG,
  input  ODD,
  input  EQ_L,
  input  EQ_H,
  input  S0,
  input  S1,
  input  S2,
  input  OPC_JMP,
  input  OPC_PFL,
  input  JMP_SENSE,
  input  ACT_ARG,
  input  INC_STAGE,
  input  OPC_PFH,
  input  ARG3,
  output ACT_JMP,
  output INT,
  output EQ,
  output ACT_PC,
  output ACT_PC_BRIDGE,
  output ACT_INST,
  output ACT_INCPL,
  output ACT_INST_BRIDGE,
  output ACT_INCPL_N,
  output ACT_INCPH,
  output PFL_CIN,
  output ACT_INCPH_N
);

  wire ic_7400_5_y;

  IC_7408 ic_7408_1 (.A(OPC_PFL), .B(INC_STAGE), .Y(ACT_INCPL));
  IC_7408 ic_7408_2 (.A(INC_STAGE), .B(OPC_PFH), .Y(ACT_INCPH));
  IC_74151 ic_74151_1 (
    .I0(1'b1), .I1(EQU), .I2(CNDX), .I3(INTM), .I4(CARRY), .I5(NEG), .I6(ODD), .I7(1'b0), .S0(S0), .S1(S1),
    .S2(S2), .E(OPC_JMP), .W(ACT_JMP));  // open: Y
  IC_7400 ic_7400_1 (.A(ACT_INCPL), .B(ACT_INCPL), .Y(ACT_INCPL_N));
  IC_7400 ic_7400_2 (.A(ACT_INCPH), .B(ACT_INCPH), .Y(ACT_INCPH_N));
  IC_7400 ic_7400_3 (.A(INTX), .B(OPC_INTSI), .Y(INT));
  IC_7408 ic_7408_3 (.A(EQ_L), .B(EQ_H), .Y(EQ));
  IC_7400 ic_7400_4 (.A(ACT_ARG), .B(ACT_ARG), .Y(ACT_PC));
  IC_7400 ic_7400_5 (.A(ACT_ARG), .B(ACT_ARG), .Y(ic_7400_5_y));
  IC_7408 ic_7408_4 (.A(ACT_PC), .B(JMP_SENSE), .Y(ACT_PC_BRIDGE));
  IC_7400 ic_7400_6 (.A(JMP_SENSE), .B(JMP_SENSE), .Y(ACT_INST_BRIDGE));
  IC_7400 ic_7400_7 (.A(ic_7400_5_y), .B(ARG3), .Y(PFL_CIN));

  assign ACT_INST = ACT_ARG;

  // Notes on the sheet:
  //   OPC_PFL: pull=up
  //   INC_STAGE: pull=up
  //   OPC_PFH: pull=up
  //   EQU: pull=up
  //   CNDX: pull=up
  //   INTM: pull=up
  //   CARRY: pull=up
  //   NEG: pull=up
  //   ODD: pull=up
  //   S0: pull=up
  //   S1: pull=up
  //   S2: pull=up
  //   OPC_JMP: pull=up
  //   JMP_SENSE: pull=up
  //   ACT_ARG: pull=up
  //   ARG3: pull=up
  //   INTX: pull=up
  //   OPC_INTSI: pull=up
  //   EQ_L: pull=up
  //   EQ_H: pull=up
endmodule
