// Logisim project Osnova8_IC_lib.circ as structural Verilog: 10 circuits, main circuit IC_74374
module IC_74374 (
  input  D0,
  input  D1,
  input  D2,
  input  D3,
  input  D4,
  input  D5,
  input  D6,
  input  D7,
  input  Cp,
  input  OE,
  output O0,
  output O1,
  output O2,
  output O3,
  output O4,
  output O5,
  output O6,
  output O7
);

  wire not_1_out, register_1_q, register_2_q, register_3_q, register_4_q, register_5_q, register_6_q,
       register_7_q, register_8_q;

  not not_1 (not_1_out, OE);
  assign O0 = not_1_out ? register_1_q : 1'bz;  // Controlled_Buffer controlled_buffer_1
  Register #(.width(1)) register_1 (.D(D0), .Q(register_1_q), .clk(Cp));  // open: en, clr
  assign O1 = not_1_out ? register_2_q : 1'bz;  // Controlled_Buffer controlled_buffer_2
  Register #(.width(1)) register_2 (.D(D1), .Q(register_2_q), .clk(Cp));  // open: en, clr
  assign O2 = not_1_out ? register_3_q : 1'bz;  // Controlled_Buffer controlled_buffer_3
  Register #(.width(1)) register_3 (.D(D2), .Q(register_3_q), .clk(Cp));  // open: en, clr
  assign O3 = not_1_out ? register_4_q : 1'bz;  // Controlled_Buffer controlled_buffer_4
  Register #(.width(1)) register_4 (.D(D3), .Q(register_4_q), .clk(Cp));  // open: en, clr
  assign O4 = not_1_out ? register_5_q : 1'bz;  // Controlled_Buffer controlled_buffer_5
  Register #(.width(1)) register_5 (.D(D4), .Q(register_5_q), .clk(Cp));  // open: en, clr
  assign O5 = not_1_out ? register_6_q : 1'bz;  // Controlled_Buffer controlled_buffer_6
  Register #(.width(1)) register_6 (.D(D5), .Q(register_6_q), .clk(Cp));  // open: en, clr
  assign O6 = not_1_out ? register_7_q : 1'bz;  // Controlled_Buffer controlled_buffer_7
  Register #(.width(1)) register_7 (.D(D6), .Q(register_7_q), .clk(Cp));  // open: en, clr
  assign O7 = not_1_out ? register_8_q : 1'bz;  // Controlled_Buffer controlled_buffer_8
  Register #(.width(1)) register_8 (.D(D7), .Q(register_8_q), .clk(Cp));  // open: en, clr

  // Notes on the sheet:
  //   D0: pull=up
  //   D1: pull=up
  //   D2: pull=up
  //   D3: pull=up
  //   D4: pull=up
  //   D5: pull=up
  //   D6: pull=up
  //   D7: pull=up
  //   Cp: pull=up
  //   OE: pull=up
endmodule

module IC_74138 (
  input  E3,
  input  E2,
  input  E1,
  input  A2,
  input  A1,
  input  A0,
  output O0,
  output O1,
  output O2,
  output O3,
  output O4,
  output O5,
  output O6,
  output O7
);

  wire and_1_out, decoder_1_out0, decoder_1_out1, decoder_2_out0, decoder_2_out1, decoder_3_out0,
       decoder_3_out1, decoder_4_out0, decoder_4_out1, decoder_5_out0, decoder_5_out1, decoder_6_out0,
       decoder_6_out1, decoder_7_out0, decoder_7_out1, not_1_out, not_2_out;

  not not_1 (not_1_out, E2);
  not not_2 (not_2_out, E1);
  Decoder decoder_1 (.out0(decoder_1_out0), .out1(decoder_1_out1), .sel(A2), .en(and_1_out));
  and and_1 (and_1_out, E3, not_1_out, not_2_out);
  Decoder decoder_2 (.out0(decoder_2_out0), .out1(decoder_2_out1), .sel(A1), .en(decoder_1_out0));
  Decoder decoder_3 (.out0(decoder_3_out0), .out1(decoder_3_out1), .sel(A1), .en(decoder_1_out1));
  Decoder decoder_4 (.out0(decoder_4_out0), .out1(decoder_4_out1), .sel(A0), .en(decoder_2_out0));
  Decoder decoder_5 (.out0(decoder_5_out0), .out1(decoder_5_out1), .sel(A0), .en(decoder_2_out1));
  Decoder decoder_6 (.out0(decoder_6_out0), .out1(decoder_6_out1), .sel(A0), .en(decoder_3_out0));
  Decoder decoder_7 (.out0(decoder_7_out0), .out1(decoder_7_out1), .sel(A0), .en(decoder_3_out1));
  not not_3 (O0, decoder_4_out0);
  not not_4 (O1, decoder_4_out1);
  not not_5 (O2, decoder_5_out0);
  not not_6 (O3, decoder_5_out1);
  not not_7 (O4, decoder_6_out0);
  not not_8 (O5, decoder_6_out1);
  not not_9 (O6, decoder_7_out0);
  not not_10 (O7, decoder_7_out1);

  // Notes on the sheet:
  //   E3: pull=up
  //   E2: pull=up
  //   E1: pull=up
  //   A2: pull=up
  //   A1: pull=up
  //   A0: pull=up
endmodule

module IC_74541 (
  input  A0,
  input  A1,
  input  A2,
  input  A3,
  input  A4,
  input  A5,
  input  A6,
  input  A7,
  input  G1,
  input  G2,
  output Y0,
  output Y1,
  output Y2,
  output Y3,
  output Y4,
  output Y5,
  output Y6,
  output Y7
);

  wire and_1_out, not_1_out, not_2_out;

  not not_1 (not_1_out, G1);
  not not_2 (not_2_out, G2);
  assign Y0 = and_1_out ? A0 : 1'bz;  // Controlled_Buffer controlled_buffer_1
  assign Y1 = and_1_out ? A1 : 1'bz;  // Controlled_Buffer controlled_buffer_2
  assign Y2 = and_1_out ? A2 : 1'bz;  // Controlled_Buffer controlled_buffer_3
  assign Y3 = and_1_out ? A3 : 1'bz;  // Controlled_Buffer controlled_buffer_4
  assign Y4 = and_1_out ? A4 : 1'bz;  // Controlled_Buffer controlled_buffer_5
  assign Y5 = and_1_out ? A5 : 1'bz;  // Controlled_Buffer controlled_buffer_6
  assign Y6 = and_1_out ? A6 : 1'bz;  // Controlled_Buffer controlled_buffer_7
  assign Y7 = and_1_out ? A7 : 1'bz;  // Controlled_Buffer controlled_buffer_8
  and and_1 (and_1_out, not_1_out, not_2_out);

  // Notes on the sheet:
  //   A0: pull=up
  //   A1: pull=up
  //   A2: pull=up
  //   A3: pull=up
  //   A4: pull=up
  //   A5: pull=up
  //   A6: pull=up
  //   A7: pull=up
  //   G1: pull=up
  //   G2: pull=up
endmodule

module IC_74283 (
  input  C0,
  input  A1,
  input  B1,
  input  A2,
  input  B2,
  input  A3,
  input  B3,
  input  A4,
  input  B4,
  output O1,
  output O2,
  output O3,
  output O4,
  output C4
);

  wire adder_1_cout, adder_2_cout, adder_3_cout;

  Adder #(.width(1)) adder_1 (.a(A1), .b(B1), .out(O1), .cin(C0), .cout(adder_1_cout));
  Adder #(.width(1)) adder_2 (.a(A2), .b(B2), .out(O2), .cin(adder_1_cout), .cout(adder_2_cout));
  Adder #(.width(1)) adder_3 (.a(A3), .b(B3), .out(O3), .cin(adder_2_cout), .cout(adder_3_cout));
  Adder #(.width(1)) adder_4 (.a(A4), .b(B4), .out(O4), .cin(adder_3_cout), .cout(C4));

  // Notes on the sheet:
  //   A1: pull=up
  //   B1: pull=up
  //   A2: pull=up
  //   B2: pull=up
  //   A3: pull=up
  //   B3: pull=up
  //   A4: pull=up
  //   B4: pull=up
  //   C0: pull=up
endmodule

module IC_74151 (
  input  I0,
  input  I1,
  input  I2,
  input  I3,
  input  I4,
  input  I5,
  input  I6,
  input  I7,
  input  S0,
  input  S1,
  input  S2,
  input  E,
  output Y,
  output W
);

  wire multiplexer_1_out, multiplexer_2_out, multiplexer_3_out, multiplexer_4_out, multiplexer_5_out,
       multiplexer_6_out, not_1_out;

  not not_1 (not_1_out, E);
  Multiplexer multiplexer_1 (.in0(I0), .in1(I1), .out(multiplexer_1_out), .sel(S0));
  Multiplexer multiplexer_2 (.in0(I2), .in1(I3), .out(multiplexer_2_out), .sel(S0));
  Multiplexer multiplexer_3 (.in0(I4), .in1(I5), .out(multiplexer_3_out), .sel(S0));
  Multiplexer multiplexer_4 (.in0(I6), .in1(I7), .out(multiplexer_4_out), .sel(S0));
  Multiplexer multiplexer_5 (.in0(multiplexer_1_out), .in1(multiplexer_2_out), .out(multiplexer_5_out), .sel(S1));
  Multiplexer multiplexer_6 (.in0(multiplexer_3_out), .in1(multiplexer_4_out), .out(multiplexer_6_out), .sel(S1));
  Multiplexer #(.enable("true")) multiplexer_7 (
    .in0(multiplexer_5_out), .in1(multiplexer_6_out), .out(Y), .sel(S2), .en(not_1_out));
  not not_2 (W, Y);

  // Notes on the sheet:
  //   I0: pull=up
  //   I1: pull=up
  //   I2: pull=up
  //   I3: pull=up
  //   I4: pull=up
  //   I5: pull=up
  //   I6: pull=up
  //   I7: pull=up
  //   S0: pull=up
  //   S1: pull=up
  //   S2: pull=up
  //   E: pull=up
endmodule

module IC_74161 (
  input  EnT,
  input  EnP,
  input  D0,
  input  D1,
  input  D2,
  input  D3,
  input  Load,
  input  Cp,
  input  Clr,
  output Q0,
  output Q1,
  output Q2,
  output Q3,
  output TC
);

  wire and_1_out, and_2_out, and_3_out, and_4_out, not_1_out, not_2_out;

  and and_1 (and_1_out, EnT, EnP);
  and and_2 (and_2_out, Q0, and_1_out);
  and and_3 (and_3_out, Q1, and_2_out);
  and and_4 (and_4_out, Q2, and_3_out);
  not not_1 (not_1_out, Load);
  not not_2 (not_2_out, Clr);
  Counter #(.max('h1), .width(1)) counter_1 (
    .load(not_1_out), .D(D0), .count(and_1_out), .Q(Q0), .clk(Cp), .clr(not_2_out));  // open: carry, up
  Counter #(.max('h1), .width(1)) counter_2 (
    .load(not_1_out), .D(D1), .count(and_2_out), .Q(Q1), .clk(Cp), .clr(not_2_out));  // open: carry, up
  Counter #(.max('h1), .width(1)) counter_3 (
    .load(not_1_out), .D(D2), .count(and_3_out), .Q(Q2), .clk(Cp), .clr(not_2_out));  // open: carry, up
  Counter #(.max('h1), .width(1)) counter_4 (
    .load(not_1_out), .D(D3), .count(and_4_out), .Q(Q3), .carry(TC), .clk(Cp), .clr(not_2_out));  // open: up

  // Notes on the sheet:
  //   EnT: pull=up
  //   EnP: pull=up
  //   D0: pull=up
  //   D1: pull=up
  //   D2: pull=up
  //   D3: pull=up
  //   Load: pull=up
  //   Cp: pull=up
  //   Clr: pull=up
endmodule

module IC_74670 (
  input  D1,
  input  D2,
  input  D3,
  input  D4,
  input  WE,
  input  WA0,
  input  WA1,
  input  RE,
  input  RA0,
  input  RA1,
  output Q1,
  output Q2,
  output Q3,
  output Q4
);

  wire and_1_out, and_2_out, and_3_out, and_4_out, and_5_out, and_6_out, and_7_out, and_8_out, not_1_out,
       not_2_out, register_1_q, register_2_q, register_3_q, register_4_q, register_5_q, register_6_q,
       register_7_q, register_8_q, register_9_q, register_10_q, register_11_q, register_12_q, register_13_q,
       register_14_q, register_15_q, register_16_q;

  not not_1 (not_1_out, WE);
  not not_2 (not_2_out, RE);
  and and_1 (and_1_out, not_1_out, ~WA0, ~WA1);  // AND_Gate
  and and_2 (and_2_out, not_2_out, ~RA0, ~RA1);  // AND_Gate
  and and_3 (and_3_out, not_1_out, WA0, ~WA1);  // AND_Gate
  and and_4 (and_4_out, not_2_out, RA0, ~RA1);  // AND_Gate
  and and_5 (and_5_out, not_1_out, ~WA0, WA1);  // AND_Gate
  and and_6 (and_6_out, not_2_out, ~RA0, RA1);  // AND_Gate
  and and_7 (and_7_out, not_1_out, WA0, WA1);
  and and_8 (and_8_out, not_2_out, RA0, RA1);
  assign Q1 = and_2_out ? register_1_q : 1'bz;  // Controlled_Buffer controlled_buffer_1
  Register #(.trigger("high"), .width(1)) register_1 (.D(D1), .Q(register_1_q), .clk(and_1_out));  // open: en, clr
  assign Q2 = and_2_out ? register_2_q : 1'bz;  // Controlled_Buffer controlled_buffer_2
  Register #(.trigger("high"), .width(1)) register_2 (.D(D2), .Q(register_2_q), .clk(and_1_out));  // open: en, clr
  assign Q3 = and_2_out ? register_3_q : 1'bz;  // Controlled_Buffer controlled_buffer_3
  Register #(.trigger("high"), .width(1)) register_3 (.D(D3), .Q(register_3_q), .clk(and_1_out));  // open: en, clr
  assign Q4 = and_2_out ? register_4_q : 1'bz;  // Controlled_Buffer controlled_buffer_4
  Register #(.trigger("high"), .width(1)) register_4 (.D(D4), .Q(register_4_q), .clk(and_1_out));  // open: en, clr
  assign Q1 = and_4_out ? register_5_q : 1'bz;  // Controlled_Buffer controlled_buffer_5
  Register #(.trigger("high"), .width(1)) register_5 (.D(D1), .Q(register_5_q), .clk(and_3_out));  // open: en, clr
  assign Q2 = and_4_out ? register_6_q : 1'bz;  // Controlled_Buffer controlled_buffer_6
  Register #(.trigger("high"), .width(1)) register_6 (.D(D2), .Q(register_6_q), .clk(and_3_out));  // open: en, clr
  assign Q3 = and_4_out ? register_7_q : 1'bz;  // Controlled_Buffer controlled_buffer_7
  Register #(.trigger("high"), .width(1)) register_7 (.D(D3), .Q(register_7_q), .clk(and_3_out));  // open: en, clr
  assign Q4 = and_4_out ? register_8_q : 1'bz;  // Controlled_Buffer controlled_buffer_8
  Register #(.trigger("high"), .width(1)) register_8 (.D(D4), .Q(register_8_q), .clk(and_3_out));  // open: en, clr
  assign Q1 = and_6_out ? register_9_q : 1'bz;  // Controlled_Buffer controlled_buffer_9
  Register #(.trigger("high"), .width(1)) register_9 (.D(D1), .Q(register_9_q), .clk(and_5_out));  // open: en, clr
  assign Q2 = and_6_out ? register_10_q : 1'bz;  // Controlled_Buffer controlled_buffer_10
  Register #(.trigger("high"), .width(1)) register_10 (.D(D2), .Q(register_10_q), .clk(and_5_out));  // open: en, clr
  assign Q3 = and_6_out ? register_11_q : 1'bz;  // Controlled_Buffer controlled_buffer_11
  Register #(.trigger("high"), .width(1)) register_11 (.D(D3), .Q(register_11_q), .clk(and_5_out));  // open: en, clr
  assign Q4 = and_6_out ? register_12_q : 1'bz;  // Controlled_Buffer controlled_buffer_12
  Register #(.trigger("high"), .width(1)) register_12 (.D(D4), .Q(register_12_q), .clk(and_5_out));  // open: en, clr
  assign Q1 = and_8_out ? register_13_q : 1'bz;  // Controlled_Buffer controlled_buffer_13
  Register #(.trigger("high"), .width(1)) register_13 (.D(D1), .Q(register_13_q), .clk(and_7_out));  // open: en, clr
  assign Q2 = and_8_out ? register_14_q : 1'bz;  // Controlled_Buffer controlled_buffer_14
  Register #(.trigger("high"), .width(1)) register_14 (.D(D2), .Q(register_14_q), .clk(and_7_out));  // open: en, clr
  assign Q3 = and_8_out ? register_15_q : 1'bz;  // Controlled_Buffer controlled_buffer_15
  Register #(.trigger("high"), .width(1)) register_15 (.D(D3), .Q(register_15_q), .clk(and_7_out));  // open: en, clr
  assign Q4 = and_8_out ? register_16_q : 1'bz;  // Controlled_Buffer controlled_buffer_16
  Register #(.trigger("high"), .width(1)) register_16 (.D(D4), .Q(register_16_q), .clk(and_7_out));  // open: en, clr

  // Notes on the sheet:
  //   D2: pull=up
  //   D3: pull=up
  //   D4: pull=up
  //   WE: pull=up
  //   WA0: pull=up
  //   WA1: pull=up
  //   RE: pull=up
  //   RA0: pull=up
  //   RA1: pull=up
  //   D1: pull=up
endmodule

module IC_74181 (
  input  B0,
  input  A0,
  input  A1,
  input  S3,
  input  B1,
  input  S2,
  input  A2,
  input  S1,
  input  B2,
  input  S0,
  input  A3,
  input  CIn,
  input  B3,
  input  M,
  output G,
  output F0,
  output COut,
  output F1,
  output P,
  output F2,
  output AEQB,
  output F3
);

  // _74181 #(.ShowInternalStructure("true")) 74181_1: pin names not known; wires that end beside it: B0, A0, S3, S2, S1, S0, CIn, M, F0, F1, F2, A1, B1, A2, B2, A3, B3, G, COut, P, AEQB, F3

  // Notes on the sheet:
  //   B0: pull=up
  //   A0: pull=up
  //   S3: pull=up
  //   S2: pull=up
  //   S1: pull=up
  //   S0: pull=up
  //   CIn: pull=up
  //   M: pull=up
  //   F0: pull=up
  //   F1: pull=up
  //   F2: pull=up
  //   A1: pull=up
  //   B1: pull=up
  //   A2: pull=up
  //   B2: pull=up
  //   A3: pull=up
  //   B3: pull=up
  //   G: pull=up
  //   COut: pull=up
  //   P: pull=up
  //   AEQB: pull=up
  //   F3: pull=up
endmodule

module IC_7400 (
  input  A,
  input  B,
  output Y
);

  nand nand_1 (Y, A, B);

  // Notes on the sheet:
  //   A: pull=up
  //   B: pull=up
  //   Y: pull=up
endmodule

module IC_7408 (
  input  A,
  input  B,
  output Y
);

  and and_1 (Y, A, B);

  // Notes on the sheet:
  //   A: pull=up
  //   B: pull=up
  //   Y: pull=up
endmodule
