// Logisim project Osnova8_chipset.circ as structural Verilog: 1 circuit, main circuit MMU
module MMU (
  input  DIn0,
  input  DIn1,
  input  DIn2,
  input  DIn3,
  input  DIn4,
  input  DIn5,
  input  DIn6,
  input  DIn7,
  input  AIn0,
  input  SPSW,
  input  AIn1,
  input  AIn2,
  input  SPSR,
  input  AIn3,
  input  SPW,
  input  AIn4,
  input  SPA0,
  input  AIn5,
  input  SPA1,
  input  AIn6,
  input  AIn7,
  input  AIn8,
  input  AIn9,
  input  AIn10,
  input  AIn11,
  input  AIn12,
  input  AIn13,
  input  AIn14,
  input  AIn15,
  input  AIn16,
  input  AIn17,
  input  AIn18,
  input  AIn19,
  output DOut0,
  output DOut1,
  output DOut2,
  output DOut3,
  output DOut4,
  output DOut5,
  output DOut6,
  output DOut7,
  output AOut0,
  output AOut1,
  output AOut2,
  output AOut3,
  output AOut4,
  output AOut5,
  output AOut6,
  output AOut7,
  output AOut8,
  output AOut9,
  output AOut10,
  output AOut11,
  output AOut12,
  output AOut13,
  output AOut14,
  output AOut15,
  output AOut16,
  output AOut17,
  output AOut18,
  output AOut19,
  output SERR
);

  wire ic_74161_1_q0, ic_74161_1_q1, ic_74161_1_q2, ic_74283_1_c4, ic_74283_2_c4, ic_74283_3_c4,
       ic_74283_4_c4, ic_74670_1_q1, ic_74670_1_q2, ic_74670_1_q3, ic_74670_1_q4, ic_74670_2_q1,
       ic_74670_2_q2, ic_74670_2_q3, ic_74670_2_q4, ic_74670_3_q1, ic_74670_3_q2, ic_74670_3_q3,
       ic_74670_3_q4, ic_74670_4_q1, ic_74670_4_q2, ic_74670_4_q3, ic_74670_4_q4, ic_74670_5_q1,
       ic_74670_5_q2, ic_74670_5_q3, ic_74670_5_q4;

  IC_74541 ic_74541_1 (
    .A0(DIn0), .A1(DIn1), .A2(DIn2), .A3(DIn3), .A4(DIn4), .A5(DIn5), .A6(DIn6), .A7(DIn7), .G1(1'b0),
    .G2(1'b0), .Y0(DOut0), .Y1(DOut1), .Y2(DOut2), .Y3(DOut3), .Y4(DOut4), .Y5(DOut5), .Y6(DOut6), .Y7(DOut7));
  IC_74161 ic_74161_1 (
    .EnT(1'b1), .EnP(1'b1), .D0(DOut0), .D1(DOut1), .D2(DOut2), .D3(DOut3), .Load(1'b0), .Cp(SPSW),
    .Clr(SPSR), .Q0(ic_74161_1_q0), .Q1(ic_74161_1_q1), .Q2(ic_74161_1_q2));  // open: Q3, TC
  IC_74670 ic_74670_1 (
    .D2(DOut2), .D3(DOut3), .D4(DOut0), .WE(SPW), .WA0(ic_74161_1_q0), .WA1(ic_74161_1_q1),
    .RE(ic_74161_1_q2), .RA0(SPA0), .RA1(SPA1), .D1(DOut1), .Q2(ic_74670_1_q2), .Q3(ic_74670_1_q3),
    .Q4(ic_74670_1_q4), .Q1(ic_74670_1_q1));
  Pull_Resistor pull_resistor_1 (.node(ic_74670_1_q4));
  Pull_Resistor pull_resistor_2 (.node(ic_74670_1_q1));
  Pull_Resistor pull_resistor_3 (.node(ic_74670_1_q2));
  IC_74670 ic_74670_2 (
    .D2(DOut6), .D3(DOut7), .D4(DOut4), .WE(SPW), .WA0(ic_74161_1_q0), .WA1(ic_74161_1_q1),
    .RE(ic_74161_1_q2), .RA0(SPA0), .RA1(SPA1), .D1(DOut5), .Q2(ic_74670_2_q2), .Q3(ic_74670_2_q3),
    .Q4(ic_74670_2_q4), .Q1(ic_74670_2_q1));
  Pull_Resistor pull_resistor_4 (.node(ic_74670_2_q4));
  Pull_Resistor pull_resistor_5 (.node(ic_74670_2_q1));
  Pull_Resistor pull_resistor_6 (.node(ic_74670_2_q2));
  IC_74670 ic_74670_3 (
    .D2(DOut2), .D3(DOut3), .D4(DOut0), .WE(SPW), .WA0(ic_74161_1_q0), .WA1(ic_74161_1_q1),
    .RE(ic_74161_1_q2), .RA0(SPA0), .RA1(SPA1), .D1(DOut1), .Q2(ic_74670_3_q2), .Q3(ic_74670_3_q3),
    .Q4(ic_74670_3_q4), .Q1(ic_74670_3_q1));
  Pull_Resistor pull_resistor_7 (.node(ic_74670_3_q4));
  Pull_Resistor pull_resistor_8 (.node(ic_74670_3_q1));
  Pull_Resistor pull_resistor_9 (.node(ic_74670_3_q2));
  IC_74670 ic_74670_4 (
    .D2(DOut6), .D3(DOut7), .D4(DOut4), .WE(SPW), .WA0(ic_74161_1_q0), .WA1(ic_74161_1_q1),
    .RE(ic_74161_1_q2), .RA0(SPA0), .RA1(SPA1), .D1(DOut5), .Q2(ic_74670_4_q2), .Q3(ic_74670_4_q3),
    .Q4(ic_74670_4_q4), .Q1(ic_74670_4_q1));
  Pull_Resistor pull_resistor_10 (.node(ic_74670_4_q4));
  Pull_Resistor pull_resistor_11 (.node(ic_74670_4_q1));
  Pull_Resistor pull_resistor_12 (.node(ic_74670_4_q2));
  IC_74670 ic_74670_5 (
    .D2(DOut2), .D3(DOut3), .D4(DOut0), .WE(SPW), .WA0(ic_74161_1_q0), .WA1(ic_74161_1_q1),
    .RE(ic_74161_1_q2), .RA0(SPA0), .RA1(SPA1), .D1(DOut1), .Q2(ic_74670_5_q2), .Q3(ic_74670_5_q3),
    .Q4(ic_74670_5_q4), .Q1(ic_74670_5_q1));
  Pull_Resistor pull_resistor_13 (.node(ic_74670_5_q4));
  Pull_Resistor pull_resistor_14 (.node(ic_74670_5_q1));
  Pull_Resistor pull_resistor_15 (.node(ic_74670_5_q2));
  Pull_Resistor pull_resistor_16 (.node(ic_74670_1_q3));
  Pull_Resistor pull_resistor_17 (.node(ic_74670_2_q3));
  Pull_Resistor pull_resistor_18 (.node(ic_74670_3_q3));
  Pull_Resistor pull_resistor_19 (.node(ic_74670_4_q3));
  Pull_Resistor pull_resistor_20 (.node(ic_74670_5_q3));
  IC_74283 ic_74283_1 (
    .A1(AIn0), .B1(ic_74670_1_q4), .A2(AIn1), .B2(ic_74670_1_q1), .A3(AIn2), .B3(ic_74670_1_q2), .A4(AIn3),
    .B4(ic_74670_1_q3), .C0(1'b0), .O1(AOut0), .O2(AOut1), .O3(AOut2), .O4(AOut3), .C4(ic_74283_1_c4));
  IC_74283 ic_74283_2 (
    .A1(AIn4), .B1(ic_74670_2_q4), .A2(AIn5), .B2(ic_74670_2_q1), .A3(AIn6), .B3(ic_74670_2_q2), .A4(AIn7),
    .B4(ic_74670_2_q3), .C0(ic_74283_1_c4), .O1(AOut4), .O2(AOut5), .O3(AOut6), .O4(AOut7), .C4(ic_74283_2_c4));
  IC_74283 ic_74283_3 (
    .A1(AIn8), .B1(ic_74670_3_q4), .A2(AIn9), .B2(ic_74670_3_q1), .A3(AIn10), .B3(ic_74670_3_q2), .A4(AIn11),
    .B4(ic_74670_3_q3), .C0(ic_74283_2_c4), .O1(AOut8), .O2(AOut9), .O3(AOut10), .O4(AOut11),
    .C4(ic_74283_3_c4));
  IC_74283 ic_74283_4 (
    .A1(AIn12), .B1(ic_74670_4_q4), .A2(AIn13), .B2(ic_74670_4_q1), .A3(AIn14), .B3(ic_74670_4_q2),
    .A4(AIn15), .B4(ic_74670_4_q3), .C0(ic_74283_3_c4), .O1(AOut12), .O2(AOut13), .O3(AOut14), .O4(AOut15),
    .C4(ic_74283_4_c4));
  IC_74283 ic_74283_5 (
    .A1(AIn16), .B1(ic_74670_5_q4), .A2(AIn17), .B2(ic_74670_5_q1), .A3(AIn18), .B3(ic_74670_5_q2),
    .A4(AIn19), .B4(ic_74670_5_q3), .C0(ic_74283_4_c4), .O1(AOut16), .O2(AOut17), .O3(AOut18), .O4(AOut19),
    .C4(SERR));

  // Notes on the sheet:
  //   AIn12: pull=up
  //   AIn13: pull=up
  //   AIn14: pull=up
  //   AIn15: pull=up
  //   AIn16: pull=up
  //   AIn17: pull=up
  //   AIn18: pull=up
  //   AIn19: pull=up
  //   AIn0: pull=up
  //   AIn1: pull=up
  //   AIn2: pull=up
  //   AIn3: pull=up
  //   AIn4: pull=up
  //   AIn5: pull=up
  //   AIn6: pull=up
  //   AIn7: pull=up
  //   AIn8: pull=up
  //   AIn9: pull=up
  //   AIn10: pull=up
  //   AIn11: pull=up
  //   DIn1: pull=up
  //   DIn2: pull=up
  //   DIn3: pull=up
  //   DIn4: pull=up
  //   DIn5: pull=up
  //   DIn6: pull=up
  //   DIn7: pull=up
  //   DIn0: pull=up
  //   SPSW: pull=up
  //   SPSR: pull=up
  //   SPW: pull=up
  //   SPA0: pull=up
  //   SPA1: pull=up
endmodule
