// Logisim project osnova8_cpu.circ as structural Verilog: 1 circuit, main circuit LOG_CPU
module LOG_CPU (
  input  [7:0] bus_in,
  input  cpu_halt,
  input  cpu_clk,
  input  cpu_int,
  input  cx_cnd,
  output [7:0] bus_out,
  output add_r,
  output add_w,
  output intc,
  output cyc_7,
  output [7:0] adr_l,
  output [7:0] adr_h,
  output [3:0] adr_sct
);

  wire act_arg, act_ir, act_n_stkh, act_n_stkl, act_opc, act_stkh, act_stkl, arg_add, arg_alu, arg_dir,
       arg_rc, arg_res, arg_sctsps, arg_stkh, arg_stkl, carry_cnd, eq_cnd, eqh_cnd, eql_cnd, inc,
       inst_ctrl_bridge, jmp, log_adder8_1_co, log_and1_1_y, log_decoder3_2_y2, log_decoder3_2_y4,
       log_decoder3_2_y6, log_nand1_1_y, log_nand1_2_y, log_nand1_4_y, neg_cnd, odd_cnd, opc_dirh, opc_dirl,
       opc_dirr, opc_inte, opc_ints, opc_jmp, opc_jmp_sense, opc_ra, opc_rb, opc_rc, opc_res, opc_sct,
       opc_sps, opc_stkh, opc_stkl, pc_ctrl, pc_ctrl_bridge, pos_cnd;
  wire [3:0] arg, log_counter4_1_value, log_register4_1_value, log_register4_2_value, log_register8_1_value;
  wire [3:3] ih;
  wire [6:1] log_alu8_1_f0;
  wire [7:0] log_adder8_1_y, log_adder8_2_y, log_buffer8_1_value, log_buffer8_2_value, log_register8_2_value,
       log_register8_5_value, log_register8_6_value, log_register8_8_value;
  wire [7:4] log_buffer8_3_value;

  LOG_REGISTER8 log_register8_1 (.DATA(bus_in), .LOAD(act_ir), .OE(1'b0), .VALUE({log_register8_1_value, arg}));
  LOG_ADDER8 log_adder8_1 (.A(adr_l), .B({8{1'b0}}), .CIN(log_nand1_2_y), .Y(log_adder8_1_y), .CO(log_adder8_1_co));
  LOG_ADDER8 log_adder8_2 (.A(adr_h), .B({8{1'b0}}), .CIN(log_adder8_1_co), .Y(log_adder8_2_y));  // open: CO
  LOG_BUFFER8 log_buffer8_1 (
    .DATA({4'b0000, ih[3], 1'b0, ih[3], 1'b0}), .OE1(pc_ctrl), .OE2(1'b0), .VALUE(log_buffer8_1_value));
  LOG_REGISTER8 log_register8_2 (.DATA(bus_in), .LOAD(opc_sps), .OE(1'b0), .VALUE(log_register8_2_value));
  LOG_NAND1 log_nand1_1 (.A(act_arg), .B(act_arg), .Y(log_nand1_1_y));
  LOG_BUFFER8 log_buffer8_2 (.DATA(bus_in), .OE1(act_arg), .OE2(inst_ctrl_bridge), .VALUE(log_buffer8_2_value));
  LOG_NAND1 log_nand1_2 (.A(log_nand1_1_y), .B(arg[3]), .Y(log_nand1_2_y));
  LOG_BUFFER8 log_buffer8_3 (
    .DATA({4'b0000, log_register8_2_value[3:0]}), .OE1(act_arg), .OE2(1'b0),
    .VALUE({log_buffer8_3_value, log_buffer8_1_value[3:0]}));
  LOG_JMP_SENSE log_jmp_sense_1 (.EN(act_arg), .DATA(log_register8_1_value), .Y15(opc_jmp_sense));
  LOG_REGISTER8 log_register8_3 (.DATA(bus_in), .LOAD(opc_res), .OE(arg_res), .VALUE(bus_out));
  LOG_REGISTER8 log_register8_4 (.DATA(bus_in), .LOAD(opc_rc), .OE(arg_rc), .VALUE(bus_out));
  LOG_REGISTER8 log_register8_5 (.DATA(bus_in), .LOAD(opc_ra), .OE(1'b0), .VALUE(log_register8_5_value));
  LOG_REGISTER8 log_register8_6 (.DATA(bus_in), .LOAD(opc_rb), .OE(1'b0), .VALUE(log_register8_6_value));
  LOG_REGISTER4 log_register4_1 (.DATA(arg), .LOAD(opc_dirl), .CLR(opc_dirr), .VALUE(log_register4_1_value));
  LOG_REGISTER4 log_register4_2 (.DATA(arg), .LOAD(opc_dirh), .CLR(opc_dirr), .VALUE(log_register4_2_value));
  LOG_DECODER3 log_decoder3_1 (
    .EN(act_arg), .DATA(arg), .Y4(arg_stkh), .Y5(arg_res), .Y6(arg_add), .Y7(arg_dir), .Y0(arg_alu),
    .Y1(arg_sctsps), .Y2(arg_rc), .Y3(arg_stkl));
  LOG_REGISTER8 log_register8_7 (
    .DATA(log_adder8_1_y), .LOAD(act_n_stkl), .OE(pc_ctrl_bridge), .VALUE(log_buffer8_2_value));
  LOG_REGISTER8 log_register8_8 (
    .DATA(log_adder8_2_y), .LOAD(act_n_stkh), .OE(pc_ctrl_bridge), .VALUE(log_register8_8_value));
  LOG_BUFFER8 log_buffer8_4 (.DATA(bus_in), .OE1(act_arg), .OE2(inst_ctrl_bridge), .VALUE(log_register8_8_value));
  LOG_FILE4 log_file4_1 (.WE(opc_sct), .DATA(bus_in), .ADR(log_buffer8_1_value[3:0]), .OE(1'b0), .VALUE(adr_sct));
  LOG_ALU8 log_alu8_1 (
    .SH(log_register4_2_value), .A(log_register8_5_value), .B(log_register8_6_value),
    .SL(log_register4_1_value), .AEQBL(eql_cnd), .F0({pos_cnd, log_alu8_1_f0, odd_cnd}), .CO(carry_cnd),
    .AEQBH(eqh_cnd));
  LOG_DECODER4 log_decoder4_1 (
    .EN(act_opc), .DATA(log_register8_1_value), .Y0(opc_sct), .Y1(opc_sps), .Y2(opc_rc), .Y3(opc_stkl),
    .Y4(opc_stkh), .Y5(opc_res), .Y6(add_w), .Y7(opc_dirr), .Y8(opc_dirl), .Y9(opc_dirh), .Y10(opc_ra),
    .Y11(opc_rb), .Y12(intc), .Y13(opc_ints), .Y14(opc_inte), .Y15(opc_jmp));
  LOG_FILE8 log_file8_1 (
    .DATA(log_buffer8_2_value), .ADR(log_buffer8_1_value[3:0]), .WE(act_stkl), .OE(1'b0), .VALUE(adr_l));
  LOG_FILE8 log_file8_2 (
    .DATA(log_register8_8_value), .ADR(log_buffer8_1_value[3:0]), .WE(act_stkh), .OE(1'b0), .VALUE(adr_h));
  LOG_BUFFER8 log_buffer8_5 (.DATA({pos_cnd, log_alu8_1_f0, odd_cnd}), .OE1(arg_alu), .OE2(1'b0), .VALUE(bus_out));
  LOG_BUFFER8 log_buffer8_6 (
    .DATA({log_register4_2_value, log_register4_1_value}), .OE1(arg_dir), .OE2(1'b0), .VALUE(bus_out));
  LOG_BUFFER8 log_buffer8_7 (.DATA(adr_l), .OE1(arg_stkl), .OE2(1'b0), .VALUE(bus_out));
  LOG_BUFFER8 log_buffer8_8 (.DATA(adr_h), .OE1(arg_stkh), .OE2(1'b0), .VALUE(bus_out));
  LOG_BUFFER8 log_buffer8_9 (
    .DATA({log_register8_2_value[3:0], adr_sct}), .OE1(arg_sctsps), .OE2(1'b0), .VALUE(bus_out));
  LOG_NAND1 log_nand1_3 (.A(pos_cnd), .B(pos_cnd), .Y(neg_cnd));
  LOG_COUNTER4 log_counter4_1 (.CIN(cpu_halt), .CLK(cpu_clk), .CLR(cyc_7), .VALUE(log_counter4_1_value));  // open: CO
  LOG_NAND1 log_nand1_4 (.A(cpu_int), .B(opc_ints), .Y(log_nand1_4_y));
  LOG_MULTIPLEXOR3 log_multiplexor3_1 (
    .D1(eq_cnd), .D2(cx_cnd), .D3(ih[3]), .D4(carry_cnd), .D5(neg_cnd), .D6(odd_cnd), .D7(1'b0), .C(arg),
    .OE(inst_ctrl_bridge), .D0(1'b1), .NEG(jmp));  // open: POS
  LOG_DECODER3 log_decoder3_2 (
    .EN(1'b0), .DATA(log_counter4_1_value), .Y4(log_decoder3_2_y4), .Y6(log_decoder3_2_y6), .Y7(cyc_7),
    .Y0(act_ir), .Y2(log_decoder3_2_y2), .Y3(act_opc));  // open: Y5, Y1
  LOG_NAND1 log_nand1_5 (.A(act_arg), .B(act_arg), .Y(pc_ctrl));
  LOG_LATCH log_latch_1 (.S(log_nand1_4_y), .R(opc_inte), .VALUE(ih[3]));
  LOG_AND1 log_and1_1 (.A(act_opc), .B(log_decoder3_2_y4), .Y(log_and1_1_y));
  LOG_AND1 log_and1_2 (.A(pc_ctrl), .B(opc_jmp_sense), .Y(pc_ctrl_bridge));
  LOG_NAND1 log_nand1_6 (.A(opc_jmp_sense), .B(opc_jmp_sense), .Y(inst_ctrl_bridge));
  LOG_AND1 log_and1_3 (.A(log_decoder3_2_y2), .B(log_and1_1_y), .Y(act_arg));
  LOG_AND1 log_and1_4 (.A(log_decoder3_2_y6), .B(jmp), .Y(inc));
  LOG_AND1 log_and1_5 (.A(eql_cnd), .B(eqh_cnd), .Y(eq_cnd));
  LOG_AND1 log_and1_6 (.A(arg_add), .B(pc_ctrl), .Y(add_r));
  LOG_AND1 log_and1_7 (.A(inc), .B(opc_stkh), .Y(act_stkh));
  LOG_AND1 log_and1_8 (.A(inc), .B(opc_stkl), .Y(act_stkl));
  LOG_NAND1 log_nand1_7 (.A(act_stkh), .B(act_stkh), .Y(act_n_stkh));
  LOG_NAND1 log_nand1_8 (.A(act_stkl), .B(act_stkl), .Y(act_n_stkl));

  // Other names for the same wires on the sheet: ih[1] = ih[3]; int_mode = ih[3]; inst_ctrl = act_arg;
  //   opc_add = add_w; opc_intc = intc

  // Notes on the sheet:
  //   cpu_int: pull=up
  //   cx_cnd: pull=up
  //   cpu_halt: pull=up
  //   cpu_clk: pull=up
  //   23.11.2025.zavrseno
  //   :'D
endmodule
