// Logisim project osnova8_ic_lib.circ as structural Verilog: 28 circuits, main circuit ic_7400
module ic_7400 (
  input  VCC,
  input  GND,
  input  A1,
  input  B1,
  input  A2,
  input  B2,
  input  A3,
  input  B3,
  input  A4,
  input  B4,
  output Y1,
  output Y2,
  output Y3,
  output Y4
);

  nand nand_1 (Y1, A1, B1);
  nand nand_2 (Y2, A2, B2);
  nand nand_3 (Y3, A3, B3);
  nand nand_4 (Y4, A4, B4);

  // Notes on the sheet:
  //   B1: pull=up
  //   A2: pull=up
  //   B2: pull=up
  //   A3: pull=up
  //   B3: pull=up
  //   A4: pull=up
  //   B4: pull=up
  //   VCC: pull=up
  //   GND: pull=up
  //   A1: pull=up
endmodule

module ic_7404 (
  input  VCC,
  input  GND,
  input  A1,
  input  A2,
  input  A3,
  input  A4,
  input  A5,
  input  A6,
  output Y1,
  output Y2,
  output Y3,
  output Y4,
  output Y5,
  output Y6
);

  not not_1 (Y1, A1);
  not not_2 (Y2, A2);
  not not_3 (Y3, A3);
  not not_4 (Y4, A4);
  not not_5 (Y5, A5);
  not not_6 (Y6, A6);

  // Notes on the sheet:
  //   A2: pull=up
  //   A3: pull=up
  //   A4: pull=up
  //   A5: pull=up
  //   A6: pull=up
  //   VCC: pull=up
  //   GND: pull=up
  //   A1: pull=up
endmodule

module ic_7408 (
  input  VCC,
  input  GND,
  input  A1,
  input  B1,
  input  A2,
  input  B2,
  input  A3,
  input  B3,
  input  A4,
  input  B4,
  output Y1,
  output Y2,
  output Y3,
  output Y4
);

  and and_1 (Y1, A1, B1);
  and and_2 (Y2, A2, B2);
  and and_3 (Y3, A3, B3);
  and and_4 (Y4, A4, B4);

  // Notes on the sheet:
  //   B1: pull=up
  //   A2: pull=up
  //   B2: pull=up
  //   A3: pull=up
  //   B3: pull=up
  //   A4: pull=up
  //   B4: pull=up
  //   VCC: pull=up
  //   GND: pull=up
  //   A1: pull=up
endmodule

module ic_74283 (
  input  VCC,
  input  GND,
  input  C0,
  input  A1,
  input  A2,
  input  A3,
  input  A4,
  input  B1,
  input  B2,
  input  B3,
  input  B4,
  output S1,
  output S2,
  output S3,
  output S4,
  output C4
);

  Adder #(.width(4)) adder_1 (.a({A4, A3, A2, A1}), .b({B4, B3, B2, B1}), .out({S4, S3, S2, S1}), .cin(C0), .cout(C4));

  // Notes on the sheet:
  //   A1: pull=up
  //   A2: pull=up
  //   A3: pull=up
  //   A4: pull=up
  //   B1: pull=up
  //   B2: pull=up
  //   B3: pull=up
  //   B4: pull=up
  //   VCC: pull=up
  //   GND: pull=up
  //   C0: pull=up
endmodule

module ic_74138 (
  input  VCC,
  input  GND,
  input  G2A,
  input  G2B,
  input  G1,
  input  A,
  input  B,
  input  C,
  output Y0,
  output Y1,
  output Y2,
  output Y3,
  output Y4,
  output Y5,
  output Y6,
  output Y7
);

  wire and_1_out, decoder_1_out0, decoder_1_out1, decoder_1_out2, decoder_1_out3, decoder_1_out4,
       decoder_1_out5, decoder_1_out6, decoder_1_out7;

  Decoder #(.select(3)) decoder_1 (
    .out0(decoder_1_out0), .out1(decoder_1_out1), .out2(decoder_1_out2), .out3(decoder_1_out3),
    .out4(decoder_1_out4), .out5(decoder_1_out5), .out6(decoder_1_out6), .out7(decoder_1_out7),
    .sel({C, B, A}), .en(and_1_out));
  and and_1 (and_1_out, ~G2A, ~G2B, G1);  // AND_Gate
  not not_1 (Y0, decoder_1_out0);
  not not_2 (Y1, decoder_1_out1);
  not not_3 (Y2, decoder_1_out2);
  not not_4 (Y3, decoder_1_out3);
  not not_5 (Y4, decoder_1_out4);
  not not_6 (Y5, decoder_1_out5);
  not not_7 (Y6, decoder_1_out6);
  not not_8 (Y7, decoder_1_out7);

  // Notes on the sheet:
  //   G2B: pull=up
  //   G1: pull=up
  //   A: pull=up
  //   B: pull=up
  //   C: pull=up
  //   VCC: pull=up
  //   GND: pull=up
  //   G2A: pull=up
endmodule

module ic_74161 (
  input  VCC,
  input  GND,
  input  LOAD,
  input  A,
  input  B,
  input  C,
  input  D,
  input  ENT,
  input  ENP,
  input  CLK,
  input  CLR,
  output QA,
  output QB,
  output QC,
  output QD,
  output RC0
);

  wire and_1_out, not_1_out, not_2_out;

  not not_1 (not_1_out, LOAD);
  and and_1 (and_1_out, ENT, ENP);
  not not_2 (not_2_out, CLR);
  Counter #(.max('hf), .width(4)) counter_1 (
    .load(not_1_out), .D({D, C, B, A}), .count(and_1_out), .Q({QD, QC, QB, QA}), .carry(RC0), .clk(CLK),
    .clr(not_2_out));  // open: up

  // Notes on the sheet:
  //   A: pull=up
  //   B: pull=up
  //   C: pull=up
  //   D: pull=up
  //   ENT: pull=up
  //   ENP: pull=up
  //   CLK: pull=up
  //   CLR: pull=up
  //   VCC: pull=up
  //   GND: pull=up
  //   LOAD: pull=up
endmodule

module ic_74181 (
  input  VCC,
  input  GND,
  input  B3,
  input  B2,
  input  B1,
  input  B0,
  input  A3,
  input  A2,
  input  A1,
  input  A0,
  input  S3,
  input  S2,
  input  S1,
  input  S0,
  input  CN,
  input  M,
  output G,
  output CN4,
  output P,
  output AEQB,
  output F3,
  output F2,
  output F1,
  output F0
);

  // _74181 #(.ShowInternalStructure("true")) 74181_1: pin names not known; wires that end beside it: VCC, GND, B0, A1, A0, B1, S3, A2, S2, B2, S1, A3, S0, B3, CN, G, M, CN4, F0, P, F1, AEQB, F2, F3

  // Notes on the sheet:
  //   B2: pull=up
  //   B1: pull=up
  //   B0: pull=up
  //   A3: pull=up
  //   A2: pull=up
  //   A1: pull=up
  //   A0: pull=up
  //   S3: pull=up
  //   S2: pull=up
  //   S1: pull=up
  //   VCC: pull=up
  //   S0: pull=up
  //   CN: pull=up
  //   M: pull=up
  //   GND: pull=up
  //   B3: pull=up
endmodule

module ic_74541 (
  input  VCC,
  input  GND,
  input  I0,
  input  I1,
  input  I2,
  input  I3,
  input  I4,
  input  I5,
  input  I6,
  input  I7,
  input  OE1,
  input  OE2,
  output Y0,
  output Y1,
  output Y2,
  output Y3,
  output Y4,
  output Y5,
  output Y6,
  output Y7
);

  wire and_1_out;

  and and_1 (and_1_out, ~OE1, ~OE2);  // AND_Gate
  assign {Y7, Y6, Y5, Y4, Y3, Y2, Y1, Y0} = and_1_out ? {I7, I6, I5, I4, I3, I2, I1, I0} : 8'bz;  // Controlled_Buffer controlled_buffer_1

  // Notes on the sheet:
  //   I1: pull=up
  //   I2: pull=up
  //   I3: pull=up
  //   I4: pull=up
  //   I5: pull=up
  //   I6: pull=up
  //   I7: pull=up
  //   OE1: pull=up
  //   OE2: pull=up
  //   VCC: pull=up
  //   GND: pull=up
  //   I0: pull=up
endmodule

module ic_74374 (
  input  VCC,
  input  GND,
  input  D0,
  input  D1,
  input  D2,
  input  D3,
  input  D4,
  input  D5,
  input  D6,
  input  D7,
  input  CP,
  input  OE,
  output O0,
  output O1,
  output O2,
  output O3,
  output O4,
  output O5,
  output O6,
  output O7
);

  wire not_1_out;
  wire [7:0] register_1_q;

  not not_1 (not_1_out, OE);
  assign {O7, O6, O5, O4, O3, O2, O1, O0} = not_1_out ? register_1_q : 8'bz;  // Controlled_Buffer controlled_buffer_1
  Register register_1 (.D({D7, D6, D5, D4, D3, D2, D1, D0}), .Q(register_1_q), .clk(CP));  // open: en, clr

  // Notes on the sheet:
  //   D1: pull=up
  //   D2: pull=up
  //   D3: pull=up
  //   D4: pull=up
  //   D5: pull=up
  //   D6: pull=up
  //   D7: pull=up
  //   CP: pull=up
  //   OE: pull=up
  //   VCC: pull=up
  //   GND: pull=up
  //   D0: pull=up
endmodule

module ic_74151 (
  input  VCC,
  input  GND,
  input  D0,
  input  D1,
  input  D2,
  input  D3,
  input  D4,
  input  D5,
  input  D6,
  input  D7,
  input  A,
  input  B,
  input  C,
  input  STROBE,
  output W,
  output Y
);

  Multiplexer #(.enable("true"), .select(3)) multiplexer_1 (
    .in0(D0), .in1(D1), .in2(D2), .in3(D3), .in4(D4), .in5(D5), .in6(D6), .in7(D7), .out(Y), .sel({C, B, A}),
    .en(STROBE));
  not not_1 (W, Y);

  // Notes on the sheet:
  //   D1: pull=up
  //   D2: pull=up
  //   D3: pull=up
  //   D4: pull=up
  //   D5: pull=up
  //   D6: pull=up
  //   D7: pull=up
  //   A: pull=up
  //   B: pull=up
  //   C: pull=up
  //   STROBE: pull=up
  //   VCC: pull=up
  //   GND: pull=up
  //   D0: pull=up
endmodule

module ic_74670 (
  input  VCC,
  input  GND,
  input  GW,
  input  D1,
  input  D2,
  input  D3,
  input  D4,
  input  WA,
  input  WB,
  input  RB,
  input  RA,
  input  GR,
  output Q1,
  output Q2,
  output Q3,
  output Q4
);

  wire and_1_out, and_2_out, and_3_out, and_4_out, and_5_out, and_6_out, and_7_out, and_8_out, and_9_out,
       and_10_out, and_11_out, and_12_out, and_13_out, and_14_out, and_15_out, and_16_out, and_17_out,
       and_18_out, and_19_out, not_1_out, not_2_out;
  wire [3:0] register_1_q, register_2_q, register_3_q, register_4_q;

  not not_1 (not_1_out, GW);
  not not_2 (not_2_out, GR);
  and and_1 (and_1_out, not_1_out, and_2_out);
  and and_2 (and_2_out, not_1_out, not_1_out);
  and and_3 (and_3_out, not_1_out, and_4_out);
  and and_4 (and_4_out, not_1_out, and_1_out);
  and and_5 (and_5_out, WA, WB);
  and and_6 (and_6_out, ~WA, WB);  // AND_Gate
  and and_7 (and_7_out, WA, ~WB);  // AND_Gate
  and and_8 (and_8_out, ~WA, ~WB);  // AND_Gate
  and and_9 (and_9_out, not_1_out, and_10_out);
  and and_10 (and_10_out, not_1_out, and_3_out);
  Register #(.trigger("high"), .width(4)) register_1 (
    .D({D4, D3, D2, D1}), .en(and_5_out), .Q(register_1_q), .clk(and_15_out));  // open: clr
  and and_11 (and_11_out, and_16_out, not_2_out);
  Register #(.trigger("high"), .width(4)) register_2 (
    .D({D4, D3, D2, D1}), .en(and_6_out), .Q(register_2_q), .clk(and_15_out));  // open: clr
  and and_12 (and_12_out, and_17_out, not_2_out);
  Register #(.trigger("high"), .width(4)) register_3 (
    .D({D4, D3, D2, D1}), .en(and_7_out), .Q(register_3_q), .clk(and_15_out));  // open: clr
  and and_13 (and_13_out, and_18_out, not_2_out);
  Register #(.trigger("high"), .width(4)) register_4 (
    .D({D4, D3, D2, D1}), .en(and_8_out), .Q(register_4_q), .clk(and_15_out));  // open: clr
  and and_14 (and_14_out, and_19_out, not_2_out);
  and and_15 (and_15_out, not_1_out, and_9_out);
  assign {Q4, Q3, Q2, Q1} = and_11_out ? register_1_q : 4'bz;  // Controlled_Buffer controlled_buffer_1
  assign {Q4, Q3, Q2, Q1} = and_12_out ? register_2_q : 4'bz;  // Controlled_Buffer controlled_buffer_2
  assign {Q4, Q3, Q2, Q1} = and_13_out ? register_3_q : 4'bz;  // Controlled_Buffer controlled_buffer_3
  assign {Q4, Q3, Q2, Q1} = and_14_out ? register_4_q : 4'bz;  // Controlled_Buffer controlled_buffer_4
  and and_16 (and_16_out, RB, RA);
  and and_17 (and_17_out, ~RB, RA);  // AND_Gate
  and and_18 (and_18_out, RB, ~RA);  // AND_Gate
  and and_19 (and_19_out, ~RB, ~RA);  // AND_Gate

  // Notes on the sheet:
  //   WA: pull=up
  //   WB: pull=up
  //   RB: pull=up
  //   RA: pull=up
  //   GR: pull=up
  //   GW: pull=up
  //   D1: pull=up
  //   D2: pull=up
  //   D3: pull=up
  //   D4: pull=up
  //   VCC: pull=up
  //   GND: pull=up
endmodule

module LOG_NAND1 (
  input  A,
  input  B,
  output Y
);

  nand nand_1 (Y, A, B);

  // Notes on the sheet:
  //   A: pull=up
  //   B: pull=up
endmodule

module LOG_NOT1 (
  input  A,
  output Y
);

  not not_1 (Y, A);

  // Notes on the sheet:
  //   A: pull=up
endmodule

module LOG_AND1 (
  input  A,
  input  B,
  output Y
);

  and and_1 (Y, A, B);

  // Notes on the sheet:
  //   A: pull=up
  //   B: pull=up
endmodule

module LOG_ADDER8 (
  input  CIN,
  input  [7:0] A,
  input  [7:0] B,
  output [7:0] Y,
  output CO
);

  Adder adder_1 (.a(A), .b(B), .out(Y), .cin(CIN), .cout(CO));

  // Notes on the sheet:
  //   A: pull=up
  //   B: pull=up
  //   CIN: pull=up
endmodule

module LOG_DECODER3 (
  input  EN,
  input  [3:0] DATA,
  output Y0,
  output Y1,
  output Y2,
  output Y3,
  output Y4,
  output Y5,
  output Y6,
  output Y7
);

  wire and_1_out, decoder_1_out0, decoder_1_out1, decoder_1_out2, decoder_1_out3, decoder_1_out4,
       decoder_1_out5, decoder_1_out6, decoder_1_out7;

  and and_1 (and_1_out, ~EN, ~DATA[3], 1'b1);  // AND_Gate
  not not_1 (Y0, decoder_1_out0);
  not not_2 (Y1, decoder_1_out1);
  not not_3 (Y2, decoder_1_out2);
  not not_4 (Y3, decoder_1_out3);
  not not_5 (Y4, decoder_1_out4);
  not not_6 (Y5, decoder_1_out5);
  not not_7 (Y6, decoder_1_out6);
  not not_8 (Y7, decoder_1_out7);
  Decoder #(.select(3)) decoder_1 (
    .out0(decoder_1_out0), .out1(decoder_1_out1), .out2(decoder_1_out2), .out3(decoder_1_out3),
    .out4(decoder_1_out4), .out5(decoder_1_out5), .out6(decoder_1_out6), .out7(decoder_1_out7),
    .sel(DATA[2:0]), .en(and_1_out));

  // Notes on the sheet:
  //   EN: pull=up
  //   DATA: pull=up
endmodule

module LOG_DECODER4 (
  input  EN,
  input  [3:0] DATA,
  output Y0,
  output Y1,
  output Y2,
  output Y3,
  output Y4,
  output Y5,
  output Y6,
  output Y7,
  output Y8,
  output Y9,
  output Y10,
  output Y11,
  output Y12,
  output Y13,
  output Y14,
  output Y15
);

  wire and_1_out, and_2_out, decoder_1_out0, decoder_1_out1, decoder_1_out2, decoder_1_out3, decoder_1_out4,
       decoder_1_out5, decoder_1_out6, decoder_1_out7, decoder_2_out0, decoder_2_out1, decoder_2_out2,
       decoder_2_out3, decoder_2_out4, decoder_2_out5, decoder_2_out6, decoder_2_out7;

  Decoder #(.select(3)) decoder_1 (
    .out0(decoder_1_out0), .out1(decoder_1_out1), .out2(decoder_1_out2), .out3(decoder_1_out3),
    .out4(decoder_1_out4), .out5(decoder_1_out5), .out6(decoder_1_out6), .out7(decoder_1_out7),
    .sel(DATA[2:0]), .en(and_1_out));
  and and_1 (and_1_out, ~EN, ~DATA[3], 1'b1);  // AND_Gate
  and and_2 (and_2_out, ~EN, ~1'b0, DATA[3]);  // AND_Gate
  Decoder #(.select(3)) decoder_2 (
    .out0(decoder_2_out0), .out1(decoder_2_out1), .out2(decoder_2_out2), .out3(decoder_2_out3),
    .out4(decoder_2_out4), .out5(decoder_2_out5), .out6(decoder_2_out6), .out7(decoder_2_out7),
    .sel(DATA[2:0]), .en(and_2_out));
  not not_1 (Y0, decoder_1_out0);
  not not_2 (Y1, decoder_1_out1);
  not not_3 (Y2, decoder_1_out2);
  not not_4 (Y3, decoder_1_out3);
  not not_5 (Y4, decoder_1_out4);
  not not_6 (Y5, decoder_1_out5);
  not not_7 (Y6, decoder_1_out6);
  not not_8 (Y7, decoder_1_out7);
  not not_9 (Y8, decoder_2_out0);
  not not_10 (Y9, decoder_2_out1);
  not not_11 (Y10, decoder_2_out2);
  not not_12 (Y11, decoder_2_out3);
  not not_13 (Y12, decoder_2_out4);
  not not_14 (Y13, decoder_2_out5);
  not not_15 (Y14, decoder_2_out6);
  not not_16 (Y15, decoder_2_out7);

  // Notes on the sheet:
  //   EN: pull=up
  //   DATA: pull=up
endmodule

module LOG_COUNTER4 (
  input  CIN,
  input  CLK,
  input  CLR,
  output [3:0] VALUE,
  output CO
);

  wire not_1_out, not_2_out;

  not not_1 (not_1_out, 1'b1);
  not not_2 (not_2_out, CLR);
  Counter #(.max('hf), .width(4)) counter_1 (
    .load(not_1_out), .count(CIN), .Q(VALUE), .carry(CO), .clk(CLK), .clr(not_2_out));  // open: D, up

  // Notes on the sheet:
  //   CIN: pull=up
  //   CLK: pull=up
  //   CLR: pull=up
endmodule

module LOG_COUNTER8 (
  input  LOAD,
  input  [7:0] DATA,
  input  CIN,
  input  CLK,
  input  CLR,
  output [7:0] VALUE,
  output CO
);

  wire not_1_out, not_2_out;

  not not_1 (not_1_out, LOAD);
  not not_2 (not_2_out, CLR);
  Counter counter_1 (
    .load(not_1_out), .D(DATA), .count(CIN), .Q(VALUE), .carry(CO), .clk(CLK), .clr(not_2_out));  // open: up

  // Notes on the sheet:
  //   DATA: pull=up
  //   CIN: pull=up
  //   CLK: pull=up
  //   CLR: pull=up
  //   LOAD: pull=up
endmodule

module LOG_LATCH (
  input  S,
  input  R,
  output VALUE
);

  wire not_1_out;
  wire [3:1] counter_1_q;

  not not_1 (not_1_out, R);
  Counter #(.max('hf), .width(4)) counter_1 (
    .load(1'b1), .D(4'b1111), .count(1'b1), .Q({counter_1_q, VALUE}), .clk(S), .clr(not_1_out));  // open: carry, up

  // Notes on the sheet:
  //   S: pull=up
  //   R: pull=up
endmodule

module LOG_ALU8 (
  input  [7:0] A,
  input  [7:0] B,
  input  [3:0] SL,
  input  [3:0] SH,
  output AEQBL,
  output [7:0] F0,
  output CO,
  output AEQBH
);

  wire ic_74181_1_cn4;

  ic_74181 ic_74181_1 (
    .B2(B[2]), .B1(B[1]), .B0(B[0]), .A3(A[3]), .A2(A[2]), .A1(A[1]), .A0(A[0]), .S3(SL[3]), .S2(SL[2]),
    .S1(SL[1]), .S0(SL[0]), .CN(SH[0]), .M(SH[1]), .B3(B[3]), .CN4(ic_74181_1_cn4), .AEQB(AEQBL), .F3(F0[3]),
    .F2(F0[2]), .F1(F0[1]), .F0(F0[0]));  // open: VCC, GND, G, P
  ic_74181 ic_74181_2 (
    .B2(B[6]), .B1(B[5]), .B0(B[4]), .A3(A[7]), .A2(A[6]), .A1(A[5]), .A0(A[4]), .S3(SL[3]), .S2(SL[2]),
    .S1(SL[1]), .S0(SL[0]), .CN(ic_74181_1_cn4), .M(SH[1]), .B3(B[7]), .CN4(CO), .AEQB(AEQBH), .F3(F0[7]),
    .F2(F0[6]), .F1(F0[5]), .F0(F0[4]));  // open: VCC, GND, G, P

  // Notes on the sheet:
  //   SH: pull=up
  //   A: pull=up
  //   B: pull=up
  //   SL: pull=up
endmodule

module LOG_BUFFER8 (
  input  [7:0] DATA,
  input  OE1,
  input  OE2,
  output [7:0] VALUE
);

  wire and_1_out;

  and and_1 (and_1_out, ~OE1, ~OE2);  // AND_Gate
  assign VALUE = and_1_out ? DATA : 8'bz;  // Controlled_Buffer controlled_buffer_1

  // Notes on the sheet:
  //   DATA: pull=up
  //   OE1: pull=up
  //   OE2: pull=up
endmodule

module LOG_REGISTER8 (
  input  [7:0] DATA,
  input  LOAD,
  input  OE,
  output [7:0] VALUE
);

  wire not_1_out;
  wire [7:0] register_1_q;

  not not_1 (not_1_out, OE);
  assign VALUE = not_1_out ? register_1_q : 8'bz;  // Controlled_Buffer controlled_buffer_1
  Register register_1 (.D(DATA), .Q(register_1_q), .clk(LOAD));  // open: en, clr

  // Notes on the sheet:
  //   DATA: pull=up
  //   LOAD: pull=up
  //   OE: pull=up
endmodule

module LOG_REGISTER4 (
  input  [3:0] DATA,
  input  LOAD,
  input  CLR,
  output [3:0] VALUE
);

  wire not_1_out, not_2_out;

  not not_1 (not_1_out, 1'b0);
  not not_2 (not_2_out, CLR);
  Counter #(.max('hf), .width(4)) counter_1 (
    .load(not_1_out), .D(DATA), .count(1'b1), .Q(VALUE), .clk(LOAD), .clr(not_2_out));  // open: carry, up

  // Notes on the sheet:
  //   DATA: pull=up
  //   LOAD: pull=up
  //   CLR: pull=up
endmodule

module LOG_MULTIPLEXOR3 (
  input  D0,
  input  D1,
  input  D2,
  input  D3,
  input  D4,
  input  D5,
  input  D6,
  input  D7,
  input  [3:0] C,
  input  OE,
  output NEG,
  output POS
);

  Multiplexer #(.enable("true"), .select(3)) multiplexer_1 (
    .in0(D0), .in1(D1), .in2(D2), .in3(D3), .in4(D4), .in5(D5), .in6(D6), .in7(D7), .out(POS), .sel(C[2:0]),
    .en(OE));
  not not_1 (NEG, POS);

  // Notes on the sheet:
  //   D1: pull=up
  //   D2: pull=up
  //   D3: pull=up
  //   D4: pull=up
  //   D5: pull=up
  //   D6: pull=up
  //   D7: pull=up
  //   C: pull=up
  //   OE: pull=up
  //   D0: pull=up
endmodule

module LOG_FILE4 (
  input  WE,
  input  [7:0] DATA,
  input  [3:0] ADR,
  input  OE,
  output [3:0] VALUE
);

  wire and_1_out, and_2_out, and_3_out, and_4_out, and_5_out, and_6_out, and_7_out, and_8_out, and_9_out,
       and_10_out, and_11_out, and_12_out, and_13_out, and_14_out, and_15_out, and_16_out, and_17_out,
       and_18_out, and_19_out, not_1_out, not_2_out;
  wire [3:0] register_1_q, register_2_q, register_3_q, register_4_q;

  not not_1 (not_1_out, WE);
  and and_1 (and_1_out, not_1_out, not_1_out);
  not not_2 (not_2_out, OE);
  and and_2 (and_2_out, not_1_out, and_3_out);
  and and_3 (and_3_out, not_1_out, and_1_out);
  and and_4 (and_4_out, not_1_out, and_5_out);
  and and_5 (and_5_out, not_1_out, and_2_out);
  Register #(.trigger("high"), .width(4)) register_1 (
    .D(DATA[3:0]), .en(and_6_out), .Q(register_1_q), .clk(and_10_out));  // open: clr
  and and_6 (and_6_out, ADR[0], ADR[1]);
  Register #(.trigger("high"), .width(4)) register_2 (
    .D(DATA[3:0]), .en(and_7_out), .Q(register_2_q), .clk(and_10_out));  // open: clr
  and and_7 (and_7_out, ~ADR[0], ADR[1]);  // AND_Gate
  Register #(.trigger("high"), .width(4)) register_3 (
    .D(DATA[3:0]), .en(and_8_out), .Q(register_3_q), .clk(and_10_out));  // open: clr
  and and_8 (and_8_out, ADR[0], ~ADR[1]);  // AND_Gate
  Register #(.trigger("high"), .width(4)) register_4 (
    .D(DATA[3:0]), .en(and_9_out), .Q(register_4_q), .clk(and_10_out));  // open: clr
  and and_9 (and_9_out, ~ADR[0], ~ADR[1]);  // AND_Gate
  and and_10 (and_10_out, not_1_out, and_11_out);
  and and_11 (and_11_out, not_1_out, and_4_out);
  assign VALUE = and_12_out ? register_1_q : 4'bz;  // Controlled_Buffer controlled_buffer_1
  and and_12 (and_12_out, and_16_out, not_2_out);
  assign VALUE = and_13_out ? register_2_q : 4'bz;  // Controlled_Buffer controlled_buffer_2
  and and_13 (and_13_out, and_17_out, not_2_out);
  assign VALUE = and_14_out ? register_3_q : 4'bz;  // Controlled_Buffer controlled_buffer_3
  and and_14 (and_14_out, and_18_out, not_2_out);
  assign VALUE = and_15_out ? register_4_q : 4'bz;  // Controlled_Buffer controlled_buffer_4
  and and_15 (and_15_out, and_19_out, not_2_out);
  and and_16 (and_16_out, ADR[2], ADR[3]);
  and and_17 (and_17_out, ~ADR[2], ADR[3]);  // AND_Gate
  and and_18 (and_18_out, ADR[2], ~ADR[3]);  // AND_Gate
  and and_19 (and_19_out, ~ADR[2], ~ADR[3]);  // AND_Gate

  // Notes on the sheet:
  //   WE: pull=up
  //   DATA: pull=up
  //   ADR: pull=up
  //   OE: pull=up
endmodule

module LOG_FILE8 (
  input  [7:0] DATA,
  input  [3:0] ADR,
  input  WE,
  input  OE,
  output [7:0] VALUE
);

  wire [7:4] undriven;

  LOG_FILE4 log_file4_1 (.WE(WE), .DATA(DATA), .ADR(ADR), .OE(OE), .VALUE(VALUE[3:0]));
  LOG_FILE4 log_file4_2 (.WE(WE), .DATA({undriven, DATA[7:4]}), .ADR(ADR), .OE(OE), .VALUE(VALUE[7:4]));

  // Notes on the sheet:
  //   DATA: pull=up
  //   ADR: pull=up
  //   WE: pull=up
  //   OE: pull=up
endmodule

module LOG_JMP_SENSE (
  input  EN,
  input  [3:0] DATA,
  output Y15
);

  wire and_1_out, decoder_1_out0, decoder_1_out1, decoder_1_out2, decoder_1_out3, decoder_1_out4,
       decoder_1_out5, decoder_1_out6, decoder_1_out7;

  and and_1 (and_1_out, ~EN, ~1'b0, DATA[3]);  // AND_Gate
  Decoder #(.select(3)) decoder_1 (
    .out0(decoder_1_out0), .out1(decoder_1_out1), .out2(decoder_1_out2), .out3(decoder_1_out3),
    .out4(decoder_1_out4), .out5(decoder_1_out5), .out6(decoder_1_out6), .out7(decoder_1_out7),
    .sel(DATA[2:0]), .en(and_1_out));
  // NOT_Gate not_1 has open pins: in=decoder_1_out0, out=open
  // NOT_Gate not_2 has open pins: in=decoder_1_out1, out=open
  // NOT_Gate not_3 has open pins: in=decoder_1_out2, out=open
  // NOT_Gate not_4 has open pins: in=decoder_1_out3, out=open
  // NOT_Gate not_5 has open pins: in=decoder_1_out4, out=open
  // NOT_Gate not_6 has open pins: in=decoder_1_out5, out=open
  // NOT_Gate not_7 has open pins: in=decoder_1_out6, out=open
  not not_8 (Y15, decoder_1_out7);

  // Notes on the sheet:
  //   EN: pull=up
  //   DATA: pull=up
endmodule
