// Logisim project new_osnova.circ as structural Verilog: 2 circuits, main circuit CPU_Osnova8
module main (
  input  FLG,
  output [3:0] out_2,
  output [3:0] out_3,
  output [7:0] out_4,
  output [7:0] out_5,
  output [3:0] out_6,
  output [3:0] out_7,
  output [7:0] out_8,
  output [7:0] out_9,
  output [3:0] out_10,
  output [3:0] out_11,
  output [3:0] out_12,
  output [3:0] out_13,
  output [3:0] out_14,
  output [3:0] out_15,
  output [3:0] out_16,
  output [3:0] out_17,
  output [3:0] out_18,
  output [3:0] out_19,
  output [3:0] out_20,
  output [3:0] out_21,
  output [3:0] out_22,
  output [3:0] out_23,
  output [3:0] out_24,
  output [3:0] out_25,
  output [3:0] out_26,
  output [3:0] out_27,
  output [3:0] out_28,
  output [3:0] out_29,
  output [7:0] out_30,
  output [3:0] out_31,
  output [7:0] out_32,
  output [3:0] out_33
);

  wire clock_1_out, INT_out, MAIN_CPU_read, not_1_out, not_2_out;
  wire [7:0] MAIN_CPU_adbl, MAIN_CPU_db_out, MAIN_ROM_data;

  Clock clock_1 (.out(clock_1_out));
  not not_1 (not_1_out, INT_out);
  Button INT (.out(INT_out));
  CPU_Osnova8 MAIN_CPU (
    .EN1(1'b1), .EN2(1'b1), .CLK(clock_1_out), .FLG(FLG), .INTI(not_1_out), .DB_IN(MAIN_CPU_db_out),
    .out_44(out_12), .out_47(out_17), .out_49(out_22), .out_50(out_27), .out_53(out_11), .out_54(out_16),
    .out_55(out_21), .out_56(out_26), .out_28(out_14), .out_31(out_19), .out_34(out_24), .out_36(out_29),
    .out_38(out_13), .out_39(out_18), .out_40(out_23), .out_41(out_28), .out_9(out_7), .out_17(out_6),
    .out_8(out_31), .out_29(out_33), .READ(MAIN_CPU_read), .out_32(out_4), .out_43(out_8),
    .ADBL(MAIN_CPU_adbl), .DB_OUT(MAIN_CPU_db_out), .out_10(out_30), .out_16(out_10), .out_19(out_15),
    .out_21(out_20), .out_23(out_25), .out_46(out_5), .out_52(out_9), .out_35(out_3), .out_42(out_2),
    .out_7(out_32));  // open: out_48, out_33, WRITE, T8CLK, T16CLK, DONE, BUSY, INTX, ADBH, ADBS, SELP, out_45, out_51, out_30, out_37
  ROM MAIN_ROM (.addr(MAIN_CPU_adbl), .data(MAIN_ROM_data));
  // IC_7408 ic_7408_1: pin names not known
  not not_2 (not_2_out, MAIN_CPU_read);
  assign MAIN_CPU_db_out = not_2_out ? MAIN_ROM_data : 8'bz;  // Controlled_Buffer controlled_buffer_1
  // IC_74181 ic_74181_1: pin names not known
  // IC_74151 ic_74151_1: pin names not known
  // IC_74670 ic_74670_1: pin names not known

  // Notes on the sheet:
  //   contents of MAIN_ROM (hex, n*v repeats v):
  //   0 8c 97
endmodule

module CPU_Osnova8 (
  input  EN1,
  input  EN2,
  input  CLK,
  input  [7:0] DB_IN,
  input  FLG,
  input  INTI,
  output [7:0] out_7,
  output [3:0] out_8,
  output [3:0] out_9,
  output [7:0] out_10,
  output READ,
  output [7:0] ADBL,
  output WRITE,
  output [7:0] ADBH,
  output [3:0] ADBS,
  output [3:0] out_16,
  output [3:0] out_17,
  output T8CLK,
  output [3:0] out_19,
  output T16CLK,
  output [3:0] out_21,
  output [7:0] DB_OUT,
  output [3:0] out_23,
  output DONE,
  output BUSY,
  output [1:0] SELP,
  output INTX,
  output [3:0] out_28,
  output [3:0] out_29,
  output [3:0] out_30,
  output [3:0] out_31,
  output [7:0] out_32,
  output [7:0] out_33,
  output [3:0] out_34,
  output [3:0] out_35,
  output [3:0] out_36,
  output [3:0] out_37,
  output [3:0] out_38,
  output [3:0] out_39,
  output [3:0] out_40,
  output [3:0] out_41,
  output [3:0] out_42,
  output [7:0] out_43,
  output [3:0] out_44,
  output [3:0] out_45,
  output [7:0] out_46,
  output [3:0] out_47,
  output [7:0] out_48,
  output [3:0] out_49,
  output [3:0] out_50,
  output [3:0] out_51,
  output [7:0] out_52,
  output [3:0] out_53,
  output [3:0] out_54,
  output [3:0] out_55,
  output [3:0] out_56
);

  wire ACT_INCP, ACT_INCPH, ACT_INCPH_N, ACT_INCPL, ACT_INCPL_N, ACT_INT, ACT_OPC, ALU_L_p7, ARG_ADD,
       ARG_ALU, ARG_DVR, ARG_PFH, ARG_PFL, ARG_RC, ARG_RESR, ARG_SFPS, BUS_CIN, BUS_M, CU_AND_A_p3,
       CU_DCD_p6, CU_DCD_p8, FLG_AEQB_H, FLG_AEQB_L, FLG_CARRY, FLG_NEG, FLG_ODD, OPC_DVRH, OPC_DVRL,
       OPC_DVRR, OPC_INTSI, OPC_JMP, OPC_PFH, OPC_PFL, OPC_PS, OPC_RA, OPC_RB, OPC_RC, OPC_RESR, OPC_SF,
       PCL_CO, PFC_AND_A_p3, PFC_AND_B_p3, PFC_MUL_p5, PFC_NAND_A_p3, PFH_ADR_L_p6, PFL_ADR_L_p6, STG_COUNT,
       STG_INST, STG_INST_BR, STG_JMP, STG_PC, STG_PC_BR;
  wire [1:0] BUS_PRA, BUS_PWA;
  wire [2:0] ALU_H_p6;
  wire [3:0] BUS_ARG, BUS_OPC, BUS_S, CU_CNT_p7, PFH_ADR_L_p5, PFL_ADR_L_p5;
  wire [3:1] ALU_L_p8, SFPS_INTC_p8;
  wire [7:0] ALU_RA_p5, ALU_RB_p5, PFH_REG_p5, PFL_REG_p5;
  wire [7:4] PFH_ADR_H_p5, PFL_ADR_H_p5, SFPS_INSTM_p4, SFPS_PCM_p4;
  wire [7:6] IEU_DVR_H_p9, SFPS_INSTM_p2;

  // IC_74161 SFPS_INTC: pin names not known; wires that end beside it: 1'b1, 1'b1, 1'b0, 4'b1111, DONE, ACT_INT, out_8, {SFPS_INTC_p8, BUSY}
  // IC_74374 SFPS_PS: pin names not known; wires that end beside it: 1'b0, {DB_IN[7:4], 4'b1111}, OPC_PS, out_10
  // IC_74670 SFPS_SF: pin names not known; wires that end beside it: 1'b0, BUS_PRA, DB_IN[3:0], OPC_SF, BUS_PWA, out_16, out_19, out_21, out_23, ADBS
  // IC_74374 ALU_RA: pin names not known; wires that end beside it: 1'b0, DB_IN, OPC_RA, out_32, ALU_RA_p5
  // IC_74374 ALU_RB: pin names not known; wires that end beside it: 1'b0, DB_IN, OPC_RB, out_43, ALU_RB_p5, ALU_RB_p5[7:4]
  // IC_74181 ALU_L: pin names not known; wires that end beside it: ALU_RA_p5[3:0], ALU_RB_p5[3:0], BUS_S, out_35, BUS_M, BUS_CIN, ALU_L_p7, {ALU_L_p8, FLG_ODD}, FLG_AEQB_L
  // IC_74181 ALU_H: pin names not known; wires that end beside it: ALU_RA_p5[7:4], BUS_S, out_42, BUS_M, ALU_L_p7, {FLG_NEG, ALU_H_p6}, FLG_AEQB_H
  // IC_74374 ALU_RC: pin names not known; wires that end beside it: ARG_RC, DB_IN, OPC_RC, out_46, FLG_CARRY, DB_OUT
  // IC_74374 ALU_RESR: pin names not known; wires that end beside it: ARG_RESR, DB_IN, OPC_RESR, out_52, DB_OUT
  // IC_74541 SFPS_PCM: pin names not known; wires that end beside it: 1'b0, {4'b1111, BUSY, 1'b0, BUSY, 1'b0}, STG_PC, {SFPS_PCM_p4, BUS_PWA, BUS_PRA}
  // IC_74541 SFPS_INSTM: pin names not known; wires that end beside it: 1'b0, {4'b1111, SFPS_INSTM_p2, SELP}, STG_INST, {SFPS_INSTM_p4, BUS_PWA, BUS_PRA}
  // IC_74541 SFPS_BUF: pin names not known; wires that end beside it: 1'b0, {SFPS_INSTM_p2, SELP, ADBS}, ARG_SFPS, DB_OUT
  // IC_74541 ALU_BUF: pin names not known; wires that end beside it: 1'b0, {FLG_NEG, ALU_H_p6, ALU_L_p8, FLG_ODD}, ARG_ALU, DB_OUT
  // IC_74374 IEU_IR: pin names not known; wires that end beside it: 1'b0, DB_IN, T8CLK, out_7, {BUS_OPC, BUS_ARG}
  // IC_74138 IEU_DCD_OPC_H: pin names not known; wires that end beside it: BUS_OPC[3], 1'b0, ACT_OPC, BUS_OPC[2:0], OPC_DVRL, OPC_DVRH, OPC_RA, OPC_RB, OPC_PS, OPC_INTSI, INTX, DONE, OPC_DVRR
  // IC_74283 PFL_ADR_L: pin names not known; wires that end beside it: STG_COUNT, ADBL[3:0], 4'b0000, out_30, PFL_ADR_L_p5, PFL_ADR_L_p6
  // IC_74283 PFL_ADR_H: pin names not known; wires that end beside it: PFL_ADR_L_p6, ADBL[7:4], 4'b0000, out_37, PFL_ADR_H_p5, PCL_CO
  // IC_74283 PFH_ADR_L: pin names not known; wires that end beside it: PCL_CO, ADBH[3:0], 4'b0000, out_45, PFH_ADR_L_p5, PFH_ADR_L_p6
  // IC_74283 PFH_ADR_H: pin names not known; wires that end beside it: PFH_ADR_L_p6, ADBH[7:4], 4'b0000, out_51, PFH_ADR_H_p5
  // IC_74138 IEU_DCD_OPC_L: pin names not known; wires that end beside it: 1'b1, BUS_OPC[3], ACT_OPC, BUS_OPC[2:0], OPC_JMP, OPC_RC, OPC_SF, OPC_PFL, OPC_PFH, OPC_RESR, WRITE
  // IC_74138 IEU_DCD_SENSE: pin names not known; wires that end beside it: 1'b1, BUS_OPC[3], STG_INST, BUS_OPC[2:0], STG_JMP
  // IC_74374 PFL_REG: pin names not known; wires that end beside it: STG_PC_BR, {PFL_ADR_H_p5, PFL_ADR_L_p5}, ACT_INCPL_N, out_33, PFL_REG_p5, BUS_PRA, PFL_REG_p5[3:0], ACT_INCPL
  // IC_74541 PFL_BUF_IN: pin names not known; wires that end beside it: 1'b0, DB_IN, STG_INST_BR, PFL_REG_p5, BUS_PRA, PFL_REG_p5[7:4], ACT_INCPL, BUS_PWA
  // IC_74374 PFH_REG: pin names not known; wires that end beside it: STG_PC_BR, {PFH_ADR_H_p5, PFH_ADR_L_p5}, ACT_INCPH_N, out_48, PFH_REG_p5, BUS_PRA, PFH_REG_p5[3:0], ACT_INCPH
  // IC_74541 PFH_BUF_IN: pin names not known; wires that end beside it: 1'b0, DB_IN, STG_INST_BR, PFH_REG_p5, BUS_PRA, PFH_REG_p5[7:4], ACT_INCPH, BUS_PWA
  // IC_74670 PFL_L: pin names not known; wires that end beside it: 1'b0, out_28, out_31, out_34, ADBL[3:0], OPC_DVRH
  // IC_74670 PFL_H: pin names not known; wires that end beside it: BUS_PWA, 1'b0, out_36, out_38, out_39, out_40, out_41, ADBL[7:4]
  // IC_74670 PFH_L: pin names not known; wires that end beside it: 1'b0, out_44, out_47, out_49, ADBH[3:0]
  // IC_74670 PFH_H: pin names not known; wires that end beside it: BUS_PWA, 1'b0, out_50, out_53, out_54, out_55, out_56, ADBH[7:4]
  // IC_74138 IEU_DCD_ARG: pin names not known; wires that end beside it: 1'b1, BUS_ARG[3], STG_INST_BR, BUS_ARG[2:0], ARG_ALU, ARG_RC, ARG_SFPS, ARG_PFL, ARG_PFH
  // IC_74161 IEU_DVR_L: pin names not known; wires that end beside it: 1'b0, 1'b0, 1'b0, BUS_ARG, out_9, ARG_RESR, ARG_ADD, ARG_DVR, BUS_S
  // IC_74161 IEU_DVR_H: pin names not known; wires that end beside it: OPC_DVRR, OPC_DVRL, 1'b0, 1'b0, 1'b0, BUS_ARG, OPC_DVRR, out_17, {IEU_DVR_H_p9, BUS_M, BUS_CIN}
  // IC_74541 PFL_BUF_OUT: pin names not known; wires that end beside it: 1'b0, ADBL, ARG_PFL, DB_OUT, CLK
  // IC_74541 PFH_BUF_OUT: pin names not known; wires that end beside it: 1'b0, ADBH, ARG_PFL, DB_OUT
  // IC_74541 IEU_DVR_BUF: pin names not known; wires that end beside it: 1'b0, {IEU_DVR_H_p9, BUS_M, BUS_CIN, BUS_S}, ARG_DVR, DB_OUT
  // IC_74161 CU_CNT: pin names not known; wires that end beside it: EN1, EN2, 1'b1, 4'b1111, 1'b1, out_29, CU_CNT_p7, T16CLK
  // IC_7408 PFC_AND_A: pin names not known; wires that end beside it: FLG_AEQB_L, FLG_AEQB_H, PFC_AND_A_p3
  // IC_7400 PFC_NAND_A: pin names not known; wires that end beside it: FLG_CARRY, FLG_CARRY, PFC_NAND_A_p3, FLG, BUSY, PFC_NAND_A_p3, FLG_NEG, FLG_ODD, 1'b0
  // IC_74151 PFC_MUL: pin names not known; wires that end beside it: 1'b1, PFC_AND_A_p3, BUS_ARG[2:0], OPC_JMP, PFC_MUL_p5
  // IC_74138 CU_DCD: pin names not known; wires that end beside it: 1'b1, 1'b0, 1'b0, CU_CNT_p7[2:0], T8CLK, CU_DCD_p6, ACT_OPC, CU_DCD_p8, ACT_INCP
  // IC_7408 CU_AND_A: pin names not known; wires that end beside it: CU_DCD_p6, ACT_OPC, CU_AND_A_p3
  // IC_7408 CU_AND_D: pin names not known; wires that end beside it: 1'b1, 1'b1
  // IC_7408 PFC_AND_B: pin names not known; wires that end beside it: ACT_INCP, PFC_MUL_p5, PFC_AND_B_p3, PFC_AND_B_p3
  // IC_7400 PFC_NAND_D: pin names not known; wires that end beside it: INTI, OPC_INTSI, ACT_INT
  // IC_7400 CU_NAND_A: pin names not known; wires that end beside it: CU_AND_A_p3, CU_DCD_p8, STG_PC
  // IC_7408 PFC_AND_C: pin names not known; wires that end beside it: OPC_PFL, ACT_INCPL
  // IC_7408 PFC_AND_D: pin names not known; wires that end beside it: PFC_AND_B_p3, OPC_PFH, ACT_INCPH
  // IC_7408 CU_AND_B: pin names not known; wires that end beside it: STG_PC, STG_JMP, STG_PC_BR, STG_PC_BR, STG_PC_BR
  // IC_7400 PFC_NAND_B: pin names not known; wires that end beside it: ACT_INCPL, ACT_INCPL, ACT_INCPL_N
  // IC_7400 PFC_NAND_C: pin names not known; wires that end beside it: ACT_INCPH, ACT_INCPH, ACT_INCPH_N
  // IC_7408 CU_AND_C: pin names not known; wires that end beside it: ARG_ADD, STG_PC_BR, READ
  // IC_7400 CU_NAND_B: pin names not known; wires that end beside it: STG_INST_BR
  // IC_7400 CU_NAND_C: pin names not known; wires that end beside it: STG_PC, STG_PC, STG_INST
  // IC_7400 CU_NAND_D: pin names not known; wires that end beside it: STG_PC, BUS_ARG[3], STG_COUNT

  // Other names for the same wires on the sheet: FLG_INTM_N = BUSY; BUS_ADS[3:0] = ADBS; BUS_SELP[1:0] = SELP;
  //   ACT_IR = T8CLK; ADD_R = READ; BUS_ADH[7:0] = ADBH; BUS_ADL[7:0] = ADBL; BUS_DATA_IN[7:0] = DB_IN;
  //   BUS_DATA_OUT[7:0] = DB_OUT; BUS_INT = INTI; FLG_X_N = FLG; OPC_ADD = WRITE; OPC_INTE = DONE; OPC_INTSX = INTX;
  //   STG_ODDCYC = T16CLK

  // Notes on the sheet:
  //   EN1: pull=up
  //   EN2: pull=up
  //   CLK: pull=up
  //   FLG: pull=up
  //   INTI: pull=up
  //   DB_IN: pull=up
  //   STG - cmbl stage
  //   ACT - cmbl action
  //   BUS - bus values
  //   OPC - inst opcodes
  //   ARG - inst arguments
  //   FLG - flags -> jmp conditions
  //   Osnova8 CPU - 28. April, 2026. by Ivan Jonjic (IJPantic on github)
endmodule
